// Logisim project HERA(multithreading).circ as structural Verilog: 50 circuits, main circuit main
module main (
);

  wire branch_processing_unit_1_branching, C_R, CLK, do_interrupt, do_jump, do_load_pc, do_override_write,
       is_interrupted_flag, keyboard0_avail, keyboard0_enable, keyboard1_avail, keyboard1_enable, ld,
       next_is_interrupted_flag, not_1_out, start_thread, str, thread_switch;
  wire [3:0] a, b, d_t, override_addr_write;
  wire [4:0] Current_Flags, Flags_Post_ALSU, saved_flags, set_flags;
  wire [6:0] I_O_tty0, I_O_tty1, keyboard0_out, keyboard1_out;
  wire [15:0] Branch_PC, CR_PC, current, D, data_override_write, handler_loc, next_PC, next_thread,
       normal_next_pc, OpCode, PC, pc_to_save, R1, R2, R3, R_14, R_a, R_b, R_d, register_bank_1_out_r1,
       register_bank_1_out_r2, register_bank_1_out_r3, register_bank_1_out_r4, register_bank_1_out_r5,
       register_bank_1_out_r6, register_bank_1_out_r7, register_bank_1_out_r8, register_bank_1_out_r9,
       register_bank_1_out_ra, register_bank_1_out_rb, register_bank_1_out_rc, register_bank_1_out_rd,
       register_bank_1_out_re, register_bank_1_out_rf, saved_pc, shadow_1_out_r1, shadow_1_out_r2,
       shadow_1_out_r3, shadow_1_out_r4, shadow_1_out_r5, shadow_1_out_r6, shadow_1_out_r7, shadow_1_out_r8,
       shadow_1_out_r9, shadow_1_out_ra, shadow_1_out_rb, shadow_1_out_rc, shadow_1_out_rd, shadow_1_out_re,
       shadow_1_out_rf, thread_init_thread_pc, W_14, W_a, W_b, W_d, W_data;

  Hex_Digit_Display hex_digit_display_1 (.value(OpCode[15:12]));  // open: dp
  Hex_Digit_Display hex_digit_display_2 (.value(W_d[15:12]));  // open: dp
  Keyboard keyboard_1 (.clk(CLK), .re(keyboard0_enable), .avail(keyboard0_avail), .data(keyboard0_out));  // open: clr
  Keyboard keyboard_2 (.clk(CLK), .re(keyboard1_enable), .avail(keyboard1_avail), .data(keyboard1_out));  // open: clr
  Hex_Digit_Display hex_digit_display_3 (.value(OpCode[11:8]));  // open: dp
  Hex_Digit_Display hex_digit_display_4 (.value(W_d[11:8]));  // open: dp
  Multiplexer #(.width(16), .enable("false")) multiplexer_1 (.in0(Branch_PC), .in1(CR_PC), .out(PC), .sel(C_R));
  Hex_Digit_Display hex_digit_display_5 (.value(OpCode[3:0]));  // open: dp
  Hex_Digit_Display hex_digit_display_6 (.value(OpCode[7:4]));  // open: dp
  Hex_Digit_Display hex_digit_display_7 (.value(W_d[3:0]));  // open: dp
  Hex_Digit_Display hex_digit_display_8 (.value(W_d[7:4]));  // open: dp
  Branch_Processing_Unit branch_processing_unit_1 (
    .Current_Counter_Value(current), .Read_b(R_b), .Flags_In(Current_Flags), .Operation_Data_In(OpCode),
    .New_Operation(Branch_PC), .Branching(branch_processing_unit_1_branching));
  interruptedFlag interruptedflag_1 (.flag_out(is_interrupted_flag), .flag_in(next_is_interrupted_flag), .clock(CLK));
  or or_1 (do_jump, C_R, branch_processing_unit_1_branching);
  Hex_Digit_Display hex_digit_display_9 (.value(R1[11:8]));  // open: dp
  Hex_Digit_Display hex_digit_display_10 (.value(R1[15:12]));  // open: dp
  not not_1 (not_1_out, do_load_pc);
  Clock Universal_Clock (.out(CLK));
  Hex_Digit_Display hex_digit_display_11 (.value(R1[7:4]));  // open: dp
  Interrupts interrupts_1 (.OPCODE(current));
  Counter #(.width(16), .max('hffff)) counter_1 (
    .load(do_load_pc), .D(next_PC), .count(not_1_out), .Q(current), .clk(CLK));  // open: carry, clr
  thread_init thread_init (.OPCODE(OpCode), .start_thread(start_thread), .thread_PC(thread_init_thread_pc));
  interruptController interruptcontroller_1 (
    .handler_loc(handler_loc), .saved_PC(saved_pc), .avail(keyboard0_avail),
    .is_interrupted_flag(is_interrupted_flag), .do_branch(do_jump), .next_PC_data(PC), .opcode(OpCode),
    .do_load_PC(do_load_pc), .normal_next_PC(normal_next_pc), .next_PC_loc(next_PC),
    .next_is_interrupted_flag(next_is_interrupted_flag), .do_interrupt(do_interrupt), .current_PC(current),
    .Flags(set_flags), .saved_flags(saved_flags), .Flags_Post_ALSU(Flags_Post_ALSU),
    .thread_switch(thread_switch), .next_thread(next_thread), .start_thread(start_thread), .clock(CLK));
  Hex_Digit_Display hex_digit_display_12 (.value(R1[3:0]));  // open: dp
  Hex_Digit_Display hex_digit_display_13 (.value(R2[15:12]));  // open: dp
  I_O I_O (.R2(R2), .OPCODE(OpCode), .TTY0(I_O_tty0), .TTY1(I_O_tty1));
  Hex_Digit_Display hex_digit_display_14 (.value(R2[11:8]));  // open: dp
  TTY tty_1 (.data(I_O_tty0), .clk(CLK));  // open: we, clr
  TTY tty_2 (.data(I_O_tty1), .clk(CLK));  // open: we, clr
  ROM #(.addrWidth(16), .dataWidth(16)) rom_1 (.addr(current), .data(OpCode));  // open: sel
  Multithreading Multithreading (
    .start_thread(start_thread), .thread_PC(thread_init_thread_pc), .CLK(CLK), .thread_switch(thread_switch),
    .next_thread(next_thread));
  Hex_Digit_Display hex_digit_display_15 (.value(R2[3:0]));  // open: dp
  Hex_Digit_Display hex_digit_display_16 (.value(R2[7:4]));  // open: dp
  Hex_Digit_Display hex_digit_display_17 (.value(R3[15:12]));  // open: dp
  CALL_RETURN call_return_1 (
    .Operation_Data_In(OpCode), .Counter_In(current), .Read_R14__FP(R_14), .Read_a(R_a), .Read_b(R_b),
    .Call_Return(C_R), .Write_b(W_b), .Write_a(W_a), .Write_R14__FP(W_14), .Counter_Out(CR_PC));
  Multiplexer #(.width(16), .enable("false")) multiplexer_2 (
    .in0(W_d), .in1(data_override_write), .out(W_data), .sel(do_override_write));
  Hex_Digit_Display hex_digit_display_18 (.value(R3[7:4]));  // open: dp
  Hex_Digit_Display hex_digit_display_19 (.value(R3[11:8]));  // open: dp
  Operation_Control operation_control_1 (
    .Operation_Data_In(OpCode), .d(d_t), .a(a), .b(b), .address_override(override_addr_write),
    .daddy(do_override_write));
  RAM_Store_Load ram_store_load_1 (
    .Operation_Data_In(OpCode), .Rb_data_in(R_b), .Load(ld), .Store(str), .address_in_RAM(D));
  Hex_Digit_Display hex_digit_display_20 (.value(R3[3:0]));  // open: dp
  LED led_1 (.in(Current_Flags[4]));
  LED led_2 (.in(Current_Flags[3]));
  LED led_3 (.in(Current_Flags[2]));
  LED led_4 (.in(Current_Flags[1]));
  LED led_5 (.in(Current_Flags[0]));
  RAM #(.addrWidth(16), .dataWidth(16), .bus("separate")) ram_1 (
    .addr(D), .din(R_d), .data(W_d), .str(str), .clk(CLK), .ld(ld));  // open: sel, clr
  ALSU alsu_1 (
    .Read_a(R_a), .Read_b(R_b), .Flags_In(Current_Flags), .Write_d(W_d), .Flags_Out(Flags_Post_ALSU),
    .Read_d(R_d), .Operation_Data_In(OpCode), .Load_Write_Data(W_d), .ld(ld), .keyboard_in0(keyboard0_out),
    .keyboard_in1(keyboard1_out), .avail_0(keyboard0_avail), .avail_1(keyboard1_avail),
    .enable_keyboard0(keyboard0_enable), .enable_keyboard1(keyboard1_enable),
    .do_override_write(do_override_write), .override_write_addr(override_addr_write),
    .data_overwrite_out(data_override_write));
  Flag_Bank flag_bank_1 (.Flags_In(set_flags), .Flags_Out(Current_Flags), .CLK(CLK));
  Register_Bank register_bank_1 (
    .CLK(CLK), .Write_d_data(W_data), .Read_a(R_a), .d(d_t), .a(a), .b(b), .Register_1(R1), .Register_2(R2),
    .Register_3(R3), .Read_d(R_d), .Read_b(R_b), .Read_R14(R_14), .Call___Return(C_R), .Write_a_data(W_a),
    .Write_b_data(W_b), .in_R1(shadow_1_out_r1), .in_R2(shadow_1_out_r2), .in_R3(shadow_1_out_r3),
    .in_R4(shadow_1_out_r4), .in_R5(shadow_1_out_r5), .in_R6(shadow_1_out_r6), .in_R7(shadow_1_out_r7),
    .in_R8(shadow_1_out_r8), .in_R9(shadow_1_out_r9), .in_Ra(shadow_1_out_ra), .in_Rb(shadow_1_out_rb),
    .in_Rc(shadow_1_out_rc), .in_Rd(shadow_1_out_rd), .in_Re(shadow_1_out_re), .in_Rf(shadow_1_out_rf),
    .out_R1(register_bank_1_out_r1), .out_R2(register_bank_1_out_r2), .out_R3(register_bank_1_out_r3),
    .out_R4(register_bank_1_out_r4), .out_R5(register_bank_1_out_r5), .out_R6(register_bank_1_out_r6),
    .out_R7(register_bank_1_out_r7), .out_R8(register_bank_1_out_r8), .out_R9(register_bank_1_out_r9),
    .out_Ra(register_bank_1_out_ra), .out_Rb(register_bank_1_out_rb), .out_Rc(register_bank_1_out_rc),
    .out_Rd(register_bank_1_out_rd), .out_Re(register_bank_1_out_re), .out_Rf(register_bank_1_out_rf),
    .opcode(OpCode), .thread_switch(thread_switch));  // open: Write_14_data
  shadow shadow_1 (
    .do_interrupt(do_interrupt), .pc_to_save(pc_to_save), .opcode(OpCode), .saved_PC_out(saved_pc),
    .handler_out(handler_loc), .in_R1(register_bank_1_out_r1), .in_R2(register_bank_1_out_r2),
    .in_R3(register_bank_1_out_r3), .in_R4(register_bank_1_out_r4), .in_R5(register_bank_1_out_r5),
    .in_R6(register_bank_1_out_r6), .in_R7(register_bank_1_out_r7), .in_R8(register_bank_1_out_r8),
    .in_R9(register_bank_1_out_r9), .in_Ra(register_bank_1_out_ra), .in_Rb(register_bank_1_out_rb),
    .in_Rc(register_bank_1_out_rc), .in_Rd(register_bank_1_out_rd), .in_Re(register_bank_1_out_re),
    .in_Rf(register_bank_1_out_rf), .out_R1(shadow_1_out_r1), .out_R2(shadow_1_out_r2),
    .out_R3(shadow_1_out_r3), .out_R4(shadow_1_out_r4), .out_R5(shadow_1_out_r5), .out_R6(shadow_1_out_r6),
    .out_R7(shadow_1_out_r7), .out_R8(shadow_1_out_r8), .out_R9(shadow_1_out_r9), .out_Ra(shadow_1_out_ra),
    .out_Rb(shadow_1_out_rb), .out_Rc(shadow_1_out_rc), .out_Rd(shadow_1_out_rd), .out_Re(shadow_1_out_re),
    .out_Rf(shadow_1_out_rf), .CLOCK(CLK), .flags_to_save(Current_Flags), .saved_flags_out(saved_flags),
    .thread_switch(thread_switch));  // open: firstswitch
  Multiplexer #(.width(16), .enable("false")) multiplexer_3 (
    .in0(normal_next_pc), .in1(current), .out(pc_to_save), .sel(thread_switch));

  // Notes on the sheet:
  //   d
  //   Current
  //   a
  //   b
  //   Branching vs Call/Return
  //   Program Counter
  //   Term Project: HERA Branching and Function Calls --Blien Habtu
  //   contents of rom_1 (hex, n*v repeats v):
  //   8802 8802 e101 f100 e201 f200 a312 9120 9230 a312 eb07 fb00 100b
  //   carry-block (F4)
  //   carry (c, or F3)
  //   overflow (v, or F2)
  //   zero (z, or F1)
  //   sign (s, or F0)
  //   RAM
endmodule

module Branch_Processing_Unit (
  input  [15:0] Current_Counter_Value,
  input  [15:0] Read_b,
  input  [15:0] Operation_Data_In,
  input  [4:0] Flags_In,
  output [15:0] New_Operation,
  output Branching
);

  wire BG, BGE, BL, BLE, BUG, BULE, comparator_1_lt, multiplexer_1_out, not_4_out, not_5_out, not_6_out,
       not_7_out;
  wire [15:0] adder_1_out, o;

  xor xor_1 (BL, Flags_In[0], Flags_In[2]);
  not not_1 (BUG, BULE);
  or or_1 (BULE, ~Flags_In[3], Flags_In[1]);  // OR_Gate
  not not_2 (BG, BLE);
  or or_2 (BLE, Flags_In[1], BL);
  not not_3 (BGE, BL);
  assign o = {{8{Operation_Data_In[7]}}, Operation_Data_In[7:0]};  // Bit_Extender bit_extender_1
  not not_4 (not_4_out, Flags_In[1]);
  not not_5 (not_5_out, Flags_In[3]);
  not not_6 (not_6_out, Flags_In[0]);
  not not_7 (not_7_out, Flags_In[2]);
  Adder #(.width(16)) adder_1 (.a(Current_Counter_Value), .b(o), .out(adder_1_out));  // open: cin, cout
  Multiplexer #(.select(4)) multiplexer_1 (
    .in0(1'b1), .in2(BL), .in3(BGE), .in4(BLE), .in5(BG), .in6(BULE), .in7(BUG), .in8(Flags_In[1]),
    .in9(not_4_out), .in10(Flags_In[3]), .in11(not_5_out), .in12(Flags_In[0]), .in13(not_6_out),
    .in14(Flags_In[2]), .in15(not_7_out), .out(multiplexer_1_out), .sel(Operation_Data_In[11:8]));  // open: in1, en
  Multiplexer #(.width(16)) multiplexer_2 (
    .in0(adder_1_out), .in1(Read_b), .out(New_Operation), .sel(Operation_Data_In[12]));  // open: en
  Comparator #(.width(4), .mode("unsigned")) comparator_1 (
    .a(Operation_Data_In[15:12]), .b(4'b0010), .lt(comparator_1_lt));  // open: gt, eq
  and and_1 (Branching, comparator_1_lt, multiplexer_1_out);

  // Other names for the same wires on the sheet: _3_0[3:0] = Operation_Data_In[3:0]; OPC[15:0] = Operation_Data_In;
  //   _7_4[3:0] = Operation_Data_In[7:4]; b[15:0] = Read_b; c[15:0] = Current_Counter_Value; F0 = Flags_In[0];
  //   F1 = Flags_In[1]; F2 = Flags_In[2]; F3 = Flags_In[3]; F4 = Flags_In[4]; _11_8[3:0] = Operation_Data_In[11:8];
  //   _15_12[3:0] = Operation_Data_In[15:12]; Register_1____Relative__0 = Operation_Data_In[12]

  // Notes on the sheet:
  //   zero (z, or F1)
  //   sign (s, or F0)
  //   overflow (v, or F2)
  //   carry (c, or F3)
  //   sign (s, or F0)
  //   carry-block (F4)
  //   zero (z, or F1)
  //   overflow (v, or F2)
  //   carry (c, or F3)
  //   zero (z, or F1)
  //   carry (c, or F3)
  //   sign (s, or F0)
  //   overflow (v, or F2)
endmodule

module Operation_Control (
  input  [3:0] address_override,
  input  daddy,
  input  [15:0] Operation_Data_In,
  output [3:0] d,
  output [3:0] a,
  output [3:0] b
);

  Multiplexer #(.width(4), .enable("false")) multiplexer_1 (
    .in0(Operation_Data_In[11:8]), .in1(address_override), .out(d), .sel(daddy));

  assign a = Operation_Data_In[7:4];
  assign b = Operation_Data_In[3:0];

  // Other names for the same wires on the sheet: _3_0[3:0] = Operation_Data_In[3:0];
  //   _7_4[3:0] = Operation_Data_In[7:4]; _11_8[3:0] = Operation_Data_In[11:8];
  //   _15_12[3:0] = Operation_Data_In[15:12]
endmodule

module CALL_RETURN (
  input  [15:0] Operation_Data_In,
  input  [15:0] Counter_In,
  input  [15:0] Read_R14__FP,
  input  [15:0] Read_a,
  input  [15:0] Read_b,
  output Call_Return,
  output [15:0] Write_b,
  output [15:0] Write_a,
  output [15:0] Write_R14__FP,
  output [15:0] Counter_Out
);

  wire C_R, comparator_2_eq, comparator_3_eq, or_1_out;

  Comparator #(.width(4)) comparator_1 (.a(4'b0010), .b(Operation_Data_In[15:12]), .eq(C_R));  // open: gt, lt
  Adder #(.width(16)) adder_1 (.a(Counter_In), .b(16'h1), .out(Write_b));  // open: cin, cout
  Comparator #(.width(4)) comparator_2 (
    .a(4'b0000), .b(Operation_Data_In[11:8]), .eq(comparator_2_eq));  // open: gt, lt
  Comparator #(.width(4)) comparator_3 (
    .a(4'b0001), .b(Operation_Data_In[11:8]), .eq(comparator_3_eq));  // open: gt, lt
  or or_1 (or_1_out, comparator_2_eq, comparator_3_eq);
  and and_1 (Call_Return, C_R, or_1_out);

  assign Counter_Out = Read_b;
  assign Write_a = Read_R14__FP;
  assign Write_R14__FP = Read_a;

  // Other names for the same wires on the sheet: FP[15:0] = Read_R14__FP; op8b[3:0] = Operation_Data_In[11:8];
  //   PC[15:0] = Counter_In; Ra[15:0] = Read_a; Rb[15:0] = Read_b

  // Notes on the sheet:
  //   Rb <- PC + 1
  //   Ra <- FP
  //   FP <- Ra
  //   PC <- Rb
  //   Neither changes any flags
endmodule

module ALSU (
  input  [15:0] Read_d,
  input  [15:0] Read_a,
  input  [15:0] Read_b,
  input  [4:0] Flags_In,
  input  [15:0] Operation_Data_In,
  input  [15:0] Load_Write_Data,
  input  ld,
  input  [6:0] keyboard_in0,
  input  [6:0] keyboard_in1,
  input  avail_0,
  input  avail_1,
  output [15:0] Write_d,
  output [4:0] Flags_Out,
  output do_override_write,
  output enable_keyboard0,
  output enable_keyboard1,
  output [3:0] override_write_addr,
  output [15:0] data_overwrite_out
);

  wire [3:0] write_addr_getavail, write_addr_getchar;
  wire [4:0] _3_0_Flags_Out, _7_4_Flags_Out, _11_8_Flags_Out, ADD_Flags_Out, AND_Flags_Out, ASL_Flags_Out,
       ASR_Flags_Out, DEC_Flags_Out, FOFF_Flags_Out, FON_and_FOF_Flags, FON_Flags_Out, FSET4_Flags_Out,
       FSET5_Flags_Out, INC_DEC_Flags_Out, INC_Flags_Out, Load_Flags_Out, LSL8_Flags_Out, LSL_Flags_Out,
       LSR8_Flags_Out, LSR_Flags_Out, MUL_Flags_Out, OR_Flags_Out, RSTRF_Flags_Out, SETHI_Flags_Out,
       SETLO_Flags_Out, SUB_Flags_Out, XOR_Flags_Out;
  wire [15:0] _3_0_Data_Out, _7_4_Data_Out, _11_8_Data_Out, ADD_Data_Out, AND_Data_Out, ASL_Data_Out,
       ASR_Data_Out, data_getavail, data_getchar, DEC_Data_Out, INC_Data_Out, INC_DEC_Data_Out,
       LSL8_Data_Out, LSL_Data_Out, LSR8_Data_Out, LSR_Data_Out, MUL_Data_Out, OR_Data_Out, SAVEF_Data_Out,
       SETHI_Data_Out, SETLO_Data_Out, SUB_Data_Out, XOR_Data_Out;

  SETLO setlo_1 (
    .Data_Out(SETLO_Data_Out), .Flags_In(Flags_In), .Flags_Out(SETLO_Flags_Out), ._0_7(Operation_Data_In[7:0]));
  SETHI sethi_1 (
    .Flags_In(Flags_In), .Data_In(Read_d), .Flags_Out(SETHI_Flags_Out), .Data_Out(SETHI_Data_Out),
    ._0_7(Operation_Data_In[7:0]));
  LSL lsl_1 (.Flags_In(Flags_In), .Flags_Out(LSL_Flags_Out), .Data_Out(LSL_Data_Out), .Data_In(Read_b));
  LSR lsr_1 (.Flags_In(Flags_In), .Flags_Out(LSR_Flags_Out), .Data_Out(LSR_Data_Out), .Data_In(Read_b));
  ASL asl_1 (.Flags_In(Flags_In), .Data_Out(ASL_Data_Out), .Flags_Out(ASL_Flags_Out), .Data_In(Read_b));
  ASR asr_1 (.Flags_In(Flags_In), .Flags_Out(ASR_Flags_Out), .Data_Out(ASR_Data_Out), .Data_In(Read_b));
  LSL8 lsl8_1 (.Flags_In(Flags_In), .Data_In(Read_b), .Flags_Out(LSL8_Flags_Out), .Data_Out(LSL8_Data_Out));
  LSR8 lsr8_1 (.Flags_In(Flags_In), .Data_In(Read_b), .Flags_Out(LSR8_Flags_Out), .Data_Out(LSR8_Data_Out));
  Multiplexer #(.select(4), .width(16), .enable("false")) multiplexer_1 (
    .in3(_7_4_Data_Out), .in5(_11_8_Data_Out), .in8(AND_Data_Out), .in9(OR_Data_Out), .in10(ADD_Data_Out),
    .in11(SUB_Data_Out), .in12(MUL_Data_Out), .in13(XOR_Data_Out), .in14(SETLO_Data_Out),
    .in15(SETHI_Data_Out), .out(Write_d), .sel(Operation_Data_In[15:12]));  // open: in0, in1, in2, in4, in6, in7
  Multiplexer #(.select(4), .width(5), .enable("false")) multiplexer_2 (
    .in3(_7_4_Flags_Out), .in4(Load_Flags_Out), .in8(AND_Flags_Out), .in9(OR_Flags_Out),
    .in10(ADD_Flags_Out), .in11(SUB_Flags_Out), .in12(MUL_Flags_Out), .in13(XOR_Flags_Out),
    .in14(SETLO_Flags_Out), .in15(SETHI_Flags_Out), .out(Flags_Out), .sel(Operation_Data_In[15:12]));  // open: in0, in1, in2, in5, in6, in7
  AND and_1 (.Flags_In(Flags_In), .a(Read_a), .b(Read_b), .Flags_Out(AND_Flags_Out), .Data_Out(AND_Data_Out));
  OR or_1 (.Flags_In(Flags_In), .a(Read_a), .b(Read_b), .Flags_Out(OR_Flags_Out), .Data_Out(OR_Data_Out));
  XOR xor_1 (.Flags_In(Flags_In), .a(Read_a), .b(Read_b), .Flags_Out(XOR_Flags_Out), .Data_Out(XOR_Data_Out));
  INC inc_1 (
    .Flags_In(Flags_In), .d(Read_d), .Flags_Out(INC_Flags_Out), .Data_Out(INC_Data_Out),
    ._7_0(Operation_Data_In[7:0]));
  DEC dec_1 (
    .Flags_In(Flags_In), .d(Read_d), .Flags_Out(DEC_Flags_Out), .Data_Out(DEC_Data_Out),
    ._7_0(Operation_Data_In[7:0]));
  Hex_Digit_Display hex_digit_display_1 (.value(Operation_Data_In[15:12]));  // open: dp
  Multiplexer #(.select(4), .width(16), .enable("false")) multiplexer_3 (
    .out(_11_8_Data_Out), .sel(Operation_Data_In[11:8]));  // open: in0, in1, in2, in3, in4, in5, in6, in7, in8, in9, in10, in11, in12, in13, in14, in15
  Multiplexer #(.select(4), .width(5), .enable("false")) multiplexer_4 (
    .out(_11_8_Flags_Out), .sel(Operation_Data_In[11:8]));  // open: in0, in1, in2, in3, in4, in5, in6, in7, in8, in9, in10, in11, in12, in13, in14, in15
  Hex_Digit_Display hex_digit_display_2 (.value(Operation_Data_In[11:8]));  // open: dp
  Multiplexer #(.width(16), .enable("false")) multiplexer_5 (
    .in0(INC_Data_Out), .in1(DEC_Data_Out), .out(INC_DEC_Data_Out), .sel(Operation_Data_In[6]));
  Multiplexer #(.width(5), .enable("false")) multiplexer_6 (
    .in0(INC_Flags_Out), .in1(DEC_Flags_Out), .out(INC_DEC_Flags_Out), .sel(Operation_Data_In[6]));
  Hex_Digit_Display hex_digit_display_3 (.value(Operation_Data_In[7:4]));  // open: dp
  ADD add_1 (.Flags_In(Flags_In), .a(Read_a), .b(Read_b), .Flags_Out(ADD_Flags_Out), .Data_Out(ADD_Data_Out));
  SUB sub_1 (.Flags_In(Flags_In), .a(Read_a), .b(Read_b), .Flags_Out(SUB_Flags_Out), .Data_Out(SUB_Data_Out));
  MUL mul_1 (.Flags_Out(MUL_Flags_Out), .Flags_In(Flags_In), .a(Read_a), .Data_Out(MUL_Data_Out), .b(Read_b));
  Hex_Digit_Display hex_digit_display_4 (.value(Operation_Data_In[3:0]));  // open: dp
  Multiplexer #(.select(4), .width(16), .enable("false")) multiplexer_7 (
    .in0(LSL_Data_Out), .in1(LSR_Data_Out), .in2(LSL8_Data_Out), .in3(LSR8_Data_Out), .in4(ASL_Data_Out),
    .in5(ASR_Data_Out), .in7(_3_0_Data_Out), .in8(INC_DEC_Data_Out), .in9(INC_DEC_Data_Out),
    .in10(INC_DEC_Data_Out), .in11(INC_DEC_Data_Out), .in12(INC_DEC_Data_Out), .in13(INC_DEC_Data_Out),
    .in14(INC_DEC_Data_Out), .in15(INC_DEC_Data_Out), .out(_7_4_Data_Out), .sel(Operation_Data_In[7:4]));  // open: in6
  Multiplexer #(.select(4), .width(5), .enable("false")) multiplexer_8 (
    .in0(LSL_Flags_Out), .in1(LSR_Flags_Out), .in2(LSL8_Flags_Out), .in3(LSR8_Flags_Out),
    .in4(ASL_Flags_Out), .in5(ASR_Flags_Out), .in6(FON_and_FOF_Flags), .in7(_3_0_Flags_Out),
    .in8(INC_DEC_Flags_Out), .in9(INC_DEC_Flags_Out), .in10(INC_DEC_Flags_Out), .in11(INC_DEC_Flags_Out),
    .in12(INC_DEC_Flags_Out), .in13(INC_DEC_Flags_Out), .in14(INC_DEC_Flags_Out), .in15(INC_DEC_Flags_Out),
    .out(_7_4_Flags_Out), .sel(Operation_Data_In[7:4]));
  FSET5 fset5_1 (._11_8(Operation_Data_In[11:8]), ._3_0(Operation_Data_In[3:0]), .Flags_Out(FSET5_Flags_Out));
  FSET4 fset4_1 (.Flags_In(Flags_In), ._3_0(Operation_Data_In[3:0]), .Flags_Out(FSET4_Flags_Out));
  Multiplexer #(.select(3), .width(5), .enable("false")) multiplexer_9 (
    .in0(FON_Flags_Out), .in2(FSET5_Flags_Out), .in4(FOFF_Flags_Out), .in6(FSET4_Flags_Out),
    .out(FON_and_FOF_Flags), .sel(Operation_Data_In[11:9]));  // open: in1, in3, in5, in7
  Load_Flags load_flags_1 (.Flags_In(Flags_In), .Load_Write_Data(Load_Write_Data), .ld(ld), .Flags_Out(Load_Flags_Out));
  GET_CHAR_KEYBOARD get_char_keyboard_1 (
    .OPCODE(Operation_Data_In), .keyboard1_in(keyboard_in0), .keyboard2_in(keyboard_in1),
    .enable_keyboard0(enable_keyboard0), .enable_keyboard1(enable_keyboard1), .data_out(data_getchar),
    .write_address(write_addr_getchar));
  Multiplexer #(.select(4), .width(16), .enable("false")) multiplexer_10 (
    .in0(SAVEF_Data_Out), .in1(SAVEF_Data_Out), .in2(SAVEF_Data_Out), .in3(SAVEF_Data_Out),
    .in4(SAVEF_Data_Out), .in5(SAVEF_Data_Out), .in6(SAVEF_Data_Out), .in7(SAVEF_Data_Out),
    .out(_3_0_Data_Out), .sel(Operation_Data_In[3:0]));  // open: in8, in9, in10, in11, in12, in13, in14, in15
  Multiplexer #(.select(4), .width(5), .enable("false")) multiplexer_11 (
    .in8(RSTRF_Flags_Out), .in9(RSTRF_Flags_Out), .in10(RSTRF_Flags_Out), .in11(RSTRF_Flags_Out),
    .in12(RSTRF_Flags_Out), .in13(RSTRF_Flags_Out), .in14(RSTRF_Flags_Out), .in15(RSTRF_Flags_Out),
    .out(_3_0_Flags_Out), .sel(Operation_Data_In[3:0]));  // open: in0, in1, in2, in3, in4, in5, in6, in7
  FON fon_1 (
    .Flags_In(Flags_In), ._11_8(Operation_Data_In[11:8]), ._3_0(Operation_Data_In[3:0]),
    .Flags_Out(FON_Flags_Out));
  FOFF foff_1 (
    .Flags_In(Flags_In), ._11_8(Operation_Data_In[11:8]), ._3_0(Operation_Data_In[3:0]),
    .Flags_Out(FOFF_Flags_Out));
  SAVEF savef_1 (.Flags_In(Flags_In), .Data_Out(SAVEF_Data_Out));
  RSTRF rstrf_1 (.Data(Read_d), .Flags_Out(RSTRF_Flags_Out));
  GET_AVAIL_KEYBOARD get_avail_keyboard_1 (
    .avail_keyboard0(avail_0), .avail_keyboard1(avail_1), .opcode(Operation_Data_In),
    .data_out(data_getavail), .write_address(write_addr_getavail));
  daddy daddy_1 (
    .opcode_in(Operation_Data_In), .write_addr_avail(write_addr_getavail),
    .write_addr_getchar(write_addr_getchar), .override_write_addr(override_write_addr),
    .do_override_write_addr(do_override_write));
  Multiplexer #(.width(16), .enable("false")) multiplexer_12 (
    .in0(data_getchar), .in1(data_getavail), .out(data_overwrite_out), .sel(Operation_Data_In[8]));

  // Other names for the same wires on the sheet: _11_8[3:0] = Operation_Data_In[11:8];
  //   opcode_In[15:0] = Operation_Data_In; _3_0[3:0] = Operation_Data_In[3:0]; _7_0[7:0] = Operation_Data_In[7:0];
  //   b3 = Operation_Data_In[3]; _7_4[3:0] = Operation_Data_In[7:4]; b6 = Operation_Data_In[6]; a[15:0] = Read_a;
  //   avail0 = avail_0; avail1 = avail_1; b[15:0] = Read_b; Data_Out[15:0] = Write_d;
  //   keyboard0_in[6:0] = keyboard_in0; keyboard1_in[6:0] = keyboard_in1; Load = ld; b8 = Operation_Data_In[8];
  //   _15_12[3:0] = Operation_Data_In[15:12]

  // Notes on the sheet:
  //   Shifts and Set Data
  //   Arithmetic Computations
  //   ROM Data
  //   Editing Flags
endmodule

module Register_Bank (
  input  CLK,
  input  [15:0] opcode,
  input  [15:0] Write_d_data,
  input  [15:0] Write_a_data,
  input  [15:0] Write_b_data,
  input  [15:0] Write_14_data,
  input  [3:0] a,
  input  [3:0] d,
  input  thread_switch,
  input  [3:0] b,
  input  Call___Return,
  input  [15:0] in_R1,
  input  [15:0] in_R2,
  input  [15:0] in_R3,
  input  [15:0] in_R4,
  input  [15:0] in_R5,
  input  [15:0] in_R6,
  input  [15:0] in_R7,
  input  [15:0] in_R8,
  input  [15:0] in_R9,
  input  [15:0] in_Ra,
  input  [15:0] in_Rb,
  input  [15:0] in_Rc,
  input  [15:0] in_Rd,
  input  [15:0] in_Re,
  input  [15:0] in_Rf,
  output [15:0] Read_d,
  output [15:0] Read_a,
  output [15:0] Read_b,
  output [15:0] Register_1,
  output [15:0] Register_2,
  output [15:0] Register_3,
  output [15:0] Read_R14,
  output [15:0] out_R1,
  output [15:0] out_R2,
  output [15:0] out_R3,
  output [15:0] out_R4,
  output [15:0] out_R5,
  output [15:0] out_R6,
  output [15:0] out_R7,
  output [15:0] out_R8,
  output [15:0] out_R9,
  output [15:0] out_Ra,
  output [15:0] out_Rb,
  output [15:0] out_Rc,
  output [15:0] out_Rd,
  output [15:0] out_Re,
  output [15:0] out_Rf
);

  wire _14_E, restore_register_1_enable_out, restore_register_2_enable_out, restore_register_3_enable_out,
       restore_register_4_enable_out, restore_register_5_enable_out, restore_register_6_enable_out,
       restore_register_7_enable_out, restore_register_8_enable_out, restore_register_9_enable_out,
       restore_register_10_enable_out, restore_register_11_enable_out, restore_register_12_enable_out,
       restore_register_13_enable_out, restore_register_14_enable_out, restore_register_15_enable_out,
       update_register_1_enable, update_register_2_enable, update_register_3_enable,
       update_register_4_enable, update_register_5_enable, update_register_6_enable,
       update_register_7_enable, update_register_8_enable, update_register_9_enable,
       update_register_10_enable, update_register_11_enable, update_register_12_enable,
       update_register_13_enable, update_register_14_enable, W1a, W1b, W1d, W2a, W2b, W2d, W3a, W3b, W3d,
       W4a, W4b, W4d, W5a, W5b, W5d, W6a, W6b, W6d, W7a, W7b, W7d, W8a, W8b, W8d, W9a, W9b, W9d, W10a, W10b,
       W10d, W11a, W11b, W11d, W12a, W12b, W12d, W13a, W13b, W13d, W14a, W14b, W14d, W15a, W15b, W15d;
  wire [15:0] _14_D, R0, restore_register_1_data_out, restore_register_2_data_out,
       restore_register_3_data_out, restore_register_4_data_out, restore_register_5_data_out,
       restore_register_6_data_out, restore_register_7_data_out, restore_register_8_data_out,
       restore_register_9_data_out, restore_register_10_data_out, restore_register_11_data_out,
       restore_register_12_data_out, restore_register_13_data_out, restore_register_14_data_out,
       restore_register_15_data_out, update_register_1_data_to_write, update_register_2_data_to_write,
       update_register_3_data_to_write, update_register_4_data_to_write, update_register_5_data_to_write,
       update_register_6_data_to_write, update_register_7_data_to_write, update_register_8_data_to_write,
       update_register_9_data_to_write, update_register_10_data_to_write, update_register_11_data_to_write,
       update_register_12_data_to_write, update_register_13_data_to_write, update_register_14_data_to_write;

  Decoder #(.select(4), .enable("false")) decoder_1 (
    .out1(W1d), .out2(W2d), .out3(W3d), .out4(W4d), .out5(W5d), .out6(W6d), .out7(W7d), .out8(W8d),
    .out9(W9d), .out10(W10d), .out11(W11d), .out12(W12d), .out13(W13d), .out14(W14d), .out15(W15d), .sel(d));  // open: out0
  Decoder #(.select(4), .enable("false")) decoder_2 (
    .out1(W1a), .out2(W2a), .out3(W3a), .out4(W4a), .out5(W5a), .out6(W6a), .out7(W7a), .out8(W8a),
    .out9(W9a), .out10(W10a), .out11(W11a), .out12(W12a), .out13(W13a), .out14(W14a), .out15(W15a), .sel(a));  // open: out0
  Multiplexer #(.width(16), .enable("false")) multiplexer_1 (
    .in0(Write_d_data), .in1(Write_14_data), .out(_14_D), .sel(Call___Return));
  Decoder #(.select(4), .enable("false")) decoder_3 (
    .out1(W1b), .out2(W2b), .out3(W3b), .out4(W4b), .out5(W5b), .out6(W6b), .out7(W7b), .out8(W8b),
    .out9(W9b), .out10(W10b), .out11(W11b), .out12(W12b), .out13(W13b), .out14(W14b), .out15(W15b), .sel(b));  // open: out0
  Multiplexer #(.enable("false")) multiplexer_2 (.in0(W14d), .in1(1'b1), .out(_14_E), .sel(Call___Return));
  Update_Register update_register_1 (
    .Write_d_data(Write_d_data), .Write_a_data(Write_a_data), .Write_b_data(Write_b_data),
    .Call___Return(Call___Return), .W_d(W1d), .W_a(W1a), .W_b(W1b),
    .Data_to_write(update_register_1_data_to_write), .Enable(update_register_1_enable));
  Update_Register update_register_2 (
    .Write_d_data(Write_d_data), .Write_a_data(Write_a_data), .Write_b_data(Write_b_data),
    .Call___Return(Call___Return), .W_d(W2d), .W_a(W2a), .W_b(W2b),
    .Data_to_write(update_register_2_data_to_write), .Enable(update_register_2_enable));
  Update_Register update_register_3 (
    .Write_d_data(Write_d_data), .Write_a_data(Write_a_data), .Write_b_data(Write_b_data),
    .Call___Return(Call___Return), .W_d(W3d), .W_a(W3a), .W_b(W3b),
    .Data_to_write(update_register_3_data_to_write), .Enable(update_register_3_enable));
  Update_Register update_register_4 (
    .Write_d_data(Write_d_data), .Write_a_data(Write_a_data), .Write_b_data(Write_b_data),
    .Call___Return(Call___Return), .W_d(W4d), .W_a(W4a), .W_b(W4b),
    .Data_to_write(update_register_4_data_to_write), .Enable(update_register_4_enable));
  Update_Register update_register_5 (
    .Write_d_data(Write_d_data), .Write_a_data(Write_a_data), .Write_b_data(Write_b_data),
    .Call___Return(Call___Return), .W_d(W5d), .W_a(W5a), .W_b(W5b),
    .Data_to_write(update_register_5_data_to_write), .Enable(update_register_5_enable));
  Update_Register update_register_6 (
    .Write_d_data(Write_d_data), .Write_a_data(Write_a_data), .Write_b_data(Write_b_data),
    .Call___Return(Call___Return), .W_d(W6d), .W_a(W6a), .W_b(W6b),
    .Data_to_write(update_register_6_data_to_write), .Enable(update_register_6_enable));
  Update_Register update_register_7 (
    .Write_d_data(Write_d_data), .Write_a_data(Write_a_data), .Write_b_data(Write_b_data),
    .Call___Return(Call___Return), .W_d(W7d), .W_a(W7a), .W_b(W7b),
    .Data_to_write(update_register_7_data_to_write), .Enable(update_register_7_enable));
  restore_register restore_register_1 (
    .thread_switch(thread_switch), .opcode(opcode), .data_normal(update_register_1_data_to_write),
    .enable_normal(update_register_1_enable), .data_saved(in_R1), .data_out(restore_register_1_data_out),
    .enable_out(restore_register_1_enable_out));
  restore_register restore_register_2 (
    .thread_switch(thread_switch), .opcode(opcode), .data_normal(update_register_2_data_to_write),
    .enable_normal(update_register_2_enable), .data_saved(in_R2), .data_out(restore_register_2_data_out),
    .enable_out(restore_register_2_enable_out));
  restore_register restore_register_3 (
    .thread_switch(thread_switch), .opcode(opcode), .data_normal(update_register_3_data_to_write),
    .enable_normal(update_register_3_enable), .data_saved(in_R3), .data_out(restore_register_3_data_out),
    .enable_out(restore_register_3_enable_out));
  restore_register restore_register_4 (
    .thread_switch(thread_switch), .opcode(opcode), .data_normal(update_register_4_data_to_write),
    .enable_normal(update_register_4_enable), .data_saved(in_R4), .data_out(restore_register_4_data_out),
    .enable_out(restore_register_4_enable_out));
  restore_register restore_register_5 (
    .thread_switch(thread_switch), .opcode(opcode), .data_normal(update_register_5_data_to_write),
    .enable_normal(update_register_5_enable), .data_saved(in_R5), .data_out(restore_register_5_data_out),
    .enable_out(restore_register_5_enable_out));
  restore_register restore_register_6 (
    .thread_switch(thread_switch), .opcode(opcode), .data_normal(update_register_6_data_to_write),
    .enable_normal(update_register_6_enable), .data_saved(in_R6), .data_out(restore_register_6_data_out),
    .enable_out(restore_register_6_enable_out));
  restore_register restore_register_7 (
    .thread_switch(thread_switch), .opcode(opcode), .data_normal(update_register_7_data_to_write),
    .enable_normal(update_register_7_enable), .data_saved(in_R7), .data_out(restore_register_7_data_out),
    .enable_out(restore_register_7_enable_out));
  Register #(.width(16)) Register_0 (.Q(R0), .clk(CLK));  // open: D, en, clr
  Register #(.width(16)) u_Register_1 (
    .D(restore_register_1_data_out), .en(restore_register_1_enable_out), .Q(out_R1), .clk(CLK));  // open: clr
  Register #(.width(16)) u_Register_2 (
    .D(restore_register_2_data_out), .en(restore_register_2_enable_out), .Q(out_R2), .clk(CLK));  // open: clr
  Register #(.width(16)) u_Register_3 (
    .D(restore_register_3_data_out), .en(restore_register_3_enable_out), .Q(out_R3), .clk(CLK));  // open: clr
  Register #(.width(16)) Register_4 (
    .D(restore_register_4_data_out), .en(restore_register_4_enable_out), .Q(out_R4), .clk(CLK));  // open: clr
  Register #(.width(16)) Register_5 (
    .D(restore_register_5_data_out), .en(restore_register_5_enable_out), .Q(out_R5), .clk(CLK));  // open: clr
  Register #(.width(16)) Register_6 (
    .D(restore_register_6_data_out), .en(restore_register_6_enable_out), .Q(out_R6), .clk(CLK));  // open: clr
  Register #(.width(16)) Register_7 (
    .D(restore_register_7_data_out), .en(restore_register_7_enable_out), .Q(out_R7), .clk(CLK));  // open: clr
  Update_Register update_register_8 (
    .Write_d_data(Write_d_data), .Write_a_data(Write_a_data), .Write_b_data(Write_b_data),
    .Call___Return(Call___Return), .W_d(W8d), .W_a(W8a), .W_b(W8b),
    .Data_to_write(update_register_8_data_to_write), .Enable(update_register_8_enable));
  Update_Register update_register_9 (
    .Write_d_data(Write_d_data), .Write_a_data(Write_a_data), .Write_b_data(Write_b_data),
    .Call___Return(Call___Return), .W_d(W9d), .W_a(W9a), .W_b(W9b),
    .Data_to_write(update_register_9_data_to_write), .Enable(update_register_9_enable));
  Update_Register update_register_10 (
    .Write_d_data(Write_d_data), .Write_a_data(Write_a_data), .Write_b_data(Write_b_data),
    .Call___Return(Call___Return), .W_d(W10d), .W_a(W10a), .W_b(W10b),
    .Data_to_write(update_register_10_data_to_write), .Enable(update_register_10_enable));
  Update_Register update_register_11 (
    .Write_d_data(Write_d_data), .Write_a_data(Write_a_data), .Write_b_data(Write_b_data),
    .Call___Return(Call___Return), .W_d(W11d), .W_a(W11a), .W_b(W11b),
    .Data_to_write(update_register_11_data_to_write), .Enable(update_register_11_enable));
  Update_Register update_register_12 (
    .Write_d_data(Write_d_data), .Write_a_data(Write_a_data), .Write_b_data(Write_b_data),
    .Call___Return(Call___Return), .W_d(W12d), .W_a(W12a), .W_b(W12b),
    .Data_to_write(update_register_12_data_to_write), .Enable(update_register_12_enable));
  Update_Register update_register_13 (
    .Write_d_data(Write_d_data), .Write_a_data(Write_a_data), .Write_b_data(Write_b_data),
    .Call___Return(Call___Return), .W_d(W13d), .W_a(W13a), .W_b(W13b),
    .Data_to_write(update_register_13_data_to_write), .Enable(update_register_13_enable));
  Update_Register update_register_14 (
    .Write_d_data(Write_d_data), .Write_a_data(Write_a_data), .Write_b_data(Write_b_data),
    .Call___Return(Call___Return), .W_d(W15d), .W_a(W15a), .W_b(W15b),
    .Data_to_write(update_register_14_data_to_write), .Enable(update_register_14_enable));
  restore_register restore_register_8 (
    .thread_switch(thread_switch), .opcode(opcode), .data_normal(update_register_8_data_to_write),
    .enable_normal(update_register_8_enable), .data_saved(in_R8), .data_out(restore_register_8_data_out),
    .enable_out(restore_register_8_enable_out));
  restore_register restore_register_9 (
    .thread_switch(thread_switch), .opcode(opcode), .data_normal(update_register_9_data_to_write),
    .enable_normal(update_register_9_enable), .data_saved(in_R9), .data_out(restore_register_9_data_out),
    .enable_out(restore_register_9_enable_out));
  restore_register restore_register_10 (
    .thread_switch(thread_switch), .opcode(opcode), .data_normal(update_register_10_data_to_write),
    .enable_normal(update_register_10_enable), .data_saved(in_Ra), .data_out(restore_register_10_data_out),
    .enable_out(restore_register_10_enable_out));
  restore_register restore_register_11 (
    .thread_switch(thread_switch), .opcode(opcode), .data_normal(update_register_11_data_to_write),
    .enable_normal(update_register_11_enable), .data_saved(in_Rb), .data_out(restore_register_11_data_out),
    .enable_out(restore_register_11_enable_out));
  restore_register restore_register_12 (
    .thread_switch(thread_switch), .opcode(opcode), .data_normal(update_register_12_data_to_write),
    .enable_normal(update_register_12_enable), .data_saved(in_Rc), .data_out(restore_register_12_data_out),
    .enable_out(restore_register_12_enable_out));
  restore_register restore_register_13 (
    .thread_switch(thread_switch), .opcode(opcode), .data_normal(update_register_13_data_to_write),
    .enable_normal(update_register_13_enable), .data_saved(in_Rd), .data_out(restore_register_13_data_out),
    .enable_out(restore_register_13_enable_out));
  restore_register restore_register_14 (
    .thread_switch(thread_switch), .opcode(opcode), .data_normal(_14_D), .enable_normal(_14_E),
    .data_saved(in_Re), .data_out(restore_register_14_data_out), .enable_out(restore_register_14_enable_out));
  restore_register restore_register_15 (
    .thread_switch(thread_switch), .opcode(opcode), .data_normal(update_register_14_data_to_write),
    .enable_normal(update_register_14_enable), .data_saved(in_Rf), .data_out(restore_register_15_data_out),
    .enable_out(restore_register_15_enable_out));
  Register #(.width(16)) Register_8 (
    .D(restore_register_8_data_out), .en(restore_register_8_enable_out), .Q(out_R8), .clk(CLK));  // open: clr
  Register #(.width(16)) Register_9 (
    .D(restore_register_9_data_out), .en(restore_register_9_enable_out), .Q(out_R9), .clk(CLK));  // open: clr
  Register #(.width(16)) Register_10 (
    .D(restore_register_10_data_out), .en(restore_register_10_enable_out), .Q(out_Ra), .clk(CLK));  // open: clr
  Register #(.width(16)) Register_11 (
    .D(restore_register_11_data_out), .en(restore_register_11_enable_out), .Q(out_Rb), .clk(CLK));  // open: clr
  Register #(.width(16)) Register_12 (
    .D(restore_register_12_data_out), .en(restore_register_12_enable_out), .Q(out_Rc), .clk(CLK));  // open: clr
  Register #(.width(16)) Register_13 (
    .D(restore_register_13_data_out), .en(restore_register_13_enable_out), .Q(out_Rd), .clk(CLK));  // open: clr
  Register #(.width(16)) Register_14 (
    .D(restore_register_14_data_out), .en(restore_register_14_enable_out), .Q(out_Re), .clk(CLK));  // open: clr
  Register #(.width(16)) Register_15 (
    .D(restore_register_15_data_out), .en(restore_register_15_enable_out), .Q(out_Rf), .clk(CLK));  // open: clr
  Multiplexer #(.select(4), .width(16)) multiplexer_3 (
    .in0(R0), .in1(out_R1), .in2(out_R2), .in3(out_R3), .in4(out_R4), .in5(out_R5), .in6(out_R6),
    .in7(out_R7), .in8(out_R8), .in9(out_R9), .in10(out_Ra), .in11(out_Rb), .in12(out_Rc), .in13(out_Rd),
    .in14(out_Re), .in15(out_Rf), .out(Read_d), .sel(d));  // open: en
  Multiplexer #(.select(4), .width(16)) multiplexer_4 (
    .in0(R0), .in1(out_R1), .in2(out_R2), .in3(out_R3), .in4(out_R4), .in5(out_R5), .in6(out_R6),
    .in7(out_R7), .in8(out_R8), .in9(out_R9), .in10(out_Ra), .in11(out_Rb), .in12(out_Rc), .in13(out_Rd),
    .in14(out_Re), .in15(out_Rf), .out(Read_a), .sel(a));  // open: en
  Multiplexer #(.select(4), .width(16)) multiplexer_5 (
    .in0(R0), .in1(out_R1), .in2(out_R2), .in3(out_R3), .in4(out_R4), .in5(out_R5), .in6(out_R6),
    .in7(out_R7), .in8(out_R8), .in9(out_R9), .in10(out_Ra), .in11(out_Rb), .in12(out_Rc), .in13(out_Rd),
    .in14(out_Re), .in15(out_Rf), .out(Read_b), .sel(b));  // open: en

  assign Read_R14 = out_Re;
  assign Register_1 = out_R1;
  assign Register_2 = out_R2;
  assign Register_3 = out_R3;

  // Other names for the same wires on the sheet: C_R = Call___Return; D14[15:0] = Write_14_data;
  //   D_t[15:0] = Write_d_data; DA[15:0] = Write_a_data; DB[15:0] = Write_b_data; R1[15:0] = out_R1;
  //   R2[15:0] = out_R2; R3[15:0] = out_R3; R4[15:0] = out_R4; R5[15:0] = out_R5; R6[15:0] = out_R6;
  //   R7[15:0] = out_R7; R8[15:0] = out_R8; R9[15:0] = out_R9; R10[15:0] = out_Ra; R11[15:0] = out_Rb;
  //   R12[15:0] = out_Rc; R13[15:0] = out_Rd; R14[15:0] = out_Re; R15[15:0] = out_Rf

  // Notes on the sheet:
  //   To Display On Main:
endmodule

module Update_Register (
  input  [15:0] Write_d_data,
  input  [15:0] Write_a_data,
  input  [15:0] Write_b_data,
  input  Call___Return,
  input  W_d,
  input  W_a,
  input  W_b,
  output [15:0] Data_to_write,
  output Enable
);

  wire and_1_out, and_2_out, and_3_out, and_4_out, or_1_out;
  wire [15:0] multiplexer_1_out;

  Multiplexer #(.width(16), .enable("false")) multiplexer_1 (
    .in0(Write_d_data), .in1(Write_a_data), .out(multiplexer_1_out), .sel(and_1_out));
  and and_1 (and_1_out, Call___Return, W_a);
  Multiplexer #(.width(16), .enable("false")) multiplexer_2 (
    .in0(multiplexer_1_out), .in1(Write_b_data), .out(Data_to_write), .sel(and_2_out));
  and and_2 (and_2_out, Call___Return, W_b);
  or or_1 (or_1_out, W_d, W_a, W_b);
  and and_3 (and_3_out, W_d, ~Call___Return);  // AND_Gate
  and and_4 (and_4_out, Call___Return, or_1_out);
  or or_2 (Enable, and_3_out, and_4_out);

  // Other names for the same wires on the sheet: C_R = Call___Return; D[15:0] = Write_d_data; Da[15:0] = Write_a_data;
  //   Db[15:0] = Write_b_data; Wa = W_a; Wb = W_b; Wd = W_d
endmodule

module RAM_Store_Load (
  input  [15:0] Operation_Data_In,
  input  [15:0] Rb_data_in,
  output Load,
  output Store,
  output [15:0] address_in_RAM
);

  wire [15:0] bit_extender_1_out;

  assign bit_extender_1_out = {{11{Operation_Data_In[12]}}, {Operation_Data_In[12], Operation_Data_In[7:4]}};  // Bit_Extender bit_extender_1
  Adder #(.width(16)) adder_1 (.a(bit_extender_1_out), .b(Rb_data_in), .out(address_in_RAM));  // open: cin, cout
  Decoder #(.select(3), .enable("false")) decoder_1 (
    .out2(Load), .out3(Store), .sel(Operation_Data_In[15:13]));  // open: out0, out1, out4, out5, out6, out7

  // Other names for the same wires on the sheet: _7_4[3:0] = Operation_Data_In[7:4];
  //   _15_12[3:0] = Operation_Data_In[15:12]; Operation[2:0] = Operation_Data_In[15:13];
  //   _3_0[3:0] = Operation_Data_In[3:0]; _11_8[3:0] = Operation_Data_In[11:8]

  // Notes on the sheet:
  //   offset
  //   sign-extending o
endmodule

module Flag_Bank (
  input  [4:0] Flags_In,
  input  CLK,
  output [4:0] Flags_Out
);

  Register #(.width(1)) register_1 (.D(Flags_In[0]), .Q(Flags_Out[0]), .clk(CLK));  // open: en, clr
  Register #(.width(1)) register_2 (.D(Flags_In[1]), .Q(Flags_Out[1]), .clk(CLK));  // open: en, clr
  Register #(.width(1)) register_3 (.D(Flags_In[2]), .Q(Flags_Out[2]), .clk(CLK));  // open: en, clr
  Register #(.width(1)) register_4 (.D(Flags_In[3]), .Q(Flags_Out[3]), .clk(CLK));  // open: en, clr
  Register #(.width(1)) register_5 (.D(Flags_In[4]), .Q(Flags_Out[4]), .clk(CLK));  // open: en, clr

  // Other names for the same wires on the sheet: F0_in = Flags_In[0]; F1_in = Flags_In[1]; F2_in = Flags_In[2];
  //   F3_in = Flags_In[3]; F4_in = Flags_In[4]; F0_out = Flags_Out[0]; F1_out = Flags_Out[1]; F2_out = Flags_Out[2];
  //   F3_out = Flags_Out[3]; F4_out = Flags_Out[4]

  // Notes on the sheet:
  //   5th flag (F4), known as “carry-block”
  //   zero (z, or F1), which is set to true when zero is produced
  //   carry (c, or F3), which indicates overflow from an unsigned operation
  //   sign (s, or F0), which is set to true when a  negative value is produced by most operations
  //   overflow (v, or F2), which indicates overflow from a signed arithmetic operation
endmodule

module Zero_Flag (
  input  [15:0] Data,
  output Zero_Out
);

  Comparator #(.width(16)) comparator_1 (.a({16{1'b0}}), .b(Data), .eq(Zero_Out));  // open: gt, lt

  // Notes on the sheet:
  //   set z , to true if the result of the operation was zero, otherwise to false.
endmodule

module Sign_Flag (
  input  [15:0] Data,
  output Sign_Out
);


  assign Sign_Out = Data[15];

  // Notes on the sheet:
  //   set s, to b15 of the result
endmodule

module ADD__Overflow_Flag (
  input  [15:0] a,
  input  [15:0] b,
  input  [15:0] write_d,
  output Overflow_Out
);

  wire comparator_1_eq, comparator_2_eq;

  Comparator #(.width(1)) comparator_1 (.a(a[15]), .b(b[15]), .eq(comparator_1_eq));  // open: gt, lt
  Comparator #(.width(1)) comparator_2 (.a(a[15]), .b(write_d[15]), .eq(comparator_2_eq));  // open: gt, lt
  and and_1 (Overflow_Out, comparator_1_eq, ~comparator_2_eq);  // AND_Gate

  // Notes on the sheet:
  //   set v, to true if there was a signed-arithemetic overflow
  //   (i.e., if the signed interpretation of bits 15-0 of their result is not equal to the sum/difference/product (respectively)
  //   of the signed interpretations of the operands), or to false if there was no overflow.
endmodule

module SUB__Overflow_Flag (
  input  [15:0] a,
  input  [15:0] b,
  input  [15:0] write_d,
  output Overflow_Out
);

  wire and_1_out, and_2_out;

  and and_1 (and_1_out, ~a[15], b[15], write_d[15]);  // AND_Gate
  and and_2 (and_2_out, a[15], ~b[15], ~write_d[15]);  // AND_Gate
  or or_1 (Overflow_Out, and_1_out, and_2_out);

  // Notes on the sheet:
  //   set v, to true if there was a signed-arithemetic overflow
  //   (i.e., if the signed interpretation of bits 15-0 of their result is not equal to the sum/difference/product (respectively)
  //   of the signed interpretations of the operands), or to false if there was no overflow.
endmodule

module SUB__Carry (
  input  [15:0] a,
  input  [15:0] b,
  output Carry_Out
);

  Comparator #(.width(16)) comparator_1 (.a(a), .b(b), .gt(Carry_Out));  // open: eq, lt

  // Notes on the sheet:
  //   Carry for SUB is true when Ra > Rb
endmodule

module MUL__Overflow_Flag (
  input  [15:0] a,
  input  [15:0] b,
  input  [15:0] write_d,
  output Overflow_Out
);

  wire xor_1_out;

  xor xor_1 (xor_1_out, a[15], b[15]);
  xor xor_2 (Overflow_Out, xor_1_out, write_d[15]);

  // Notes on the sheet:
  //   set v, to true if there was a signed-arithemetic overflow
  //   (i.e., if the signed interpretation of bits 15-0 of their result is not equal to the sum/difference/product (respectively)
  //   of the signed interpretations of the operands), or to false if there was no overflow.
endmodule

module MUL__Carry (
  input  [15:0] High_Word,
  output Carry_Out
);

  wire comparator_1_eq;

  Comparator #(.width(16)) comparator_1 (.a(High_Word), .b({16{1'b0}}), .eq(comparator_1_eq));  // open: gt, lt
  not not_1 (Carry_Out, comparator_1_eq);
endmodule

module SETLO (
  input  [4:0] Flags_In,
  input  [7:0] _0_7,
  output [4:0] Flags_Out,
  output [15:0] Data_Out
);


  assign Data_Out = {{9{_0_7[7]}}, _0_7[6:0]};
  assign Flags_Out = Flags_In;

  // Other names for the same wires on the sheet: F0_in = Flags_In[0]; F1_in = Flags_In[1]; F2_in = Flags_In[2];
  //   F3_in = Flags_In[3]; F4_in = Flags_In[4]

  // Notes on the sheet:
  //   sign (s, or F0)
  //   carry-block (F4)
  //   zero (z, or F1)
  //   overflow (v, or F2)
  //   carry (c, or F3)
  //   SETLO and SETHI do not affect any flags; their actions are not affected by any flag values.
endmodule

module SETHI (
  input  [4:0] Flags_In,
  input  [15:0] Data_In,
  input  [7:0] _0_7,
  output [4:0] Flags_Out,
  output [15:0] Data_Out
);


  assign Data_Out = {_0_7, Data_In[7:0]};
  assign Flags_Out = Flags_In;

  // Other names for the same wires on the sheet: F0_in = Flags_In[0]; F1_in = Flags_In[1]; F2_in = Flags_In[2];
  //   F3_in = Flags_In[3]; F4_in = Flags_In[4]

  // Notes on the sheet:
  //   sign (s, or F0)
  //   carry-block (F4)
  //   zero (z, or F1)
  //   carry (c, or F3)
  //   SETLO and SETHI do not affect any flags; their actions are not affected by any flag values.
  //   overflow (v, or F2)
endmodule

module AND (
  input  [4:0] Flags_In,
  input  [15:0] a,
  input  [15:0] b,
  output [4:0] Flags_Out,
  output [15:0] Data_Out
);

  assign Data_Out = a & b;  // AND_Gate and_1, 16 bits wide
  Sign_Flag sign_flag_1 (.Sign_Out(Flags_Out[0]));  // open: Data
  Zero_Flag zero_flag_1 (.Zero_Out(Flags_Out[1]));  // open: Data
  Sign_Flag sign_flag_2 (.Data(Data_Out), .Sign_Out(Flags_Out[0]));
  Zero_Flag zero_flag_2 (.Data(Data_Out), .Zero_Out(Flags_Out[1]));

  assign Flags_Out[4:2] = Flags_In[4:2];

  // Other names for the same wires on the sheet: F0_in = Flags_In[0]; F1_in = Flags_In[1]; F0_out = Flags_Out[0];
  //   F1_out = Flags_Out[1]; F2_in = Flags_In[2]; F3_in = Flags_In[3]; F4_in = Flags_In[4]

  // Notes on the sheet:
  //   sign (s, or F0)
  //   carry-block (F4)
  //   zero (z, or F1)
  //   carry (c, or F3)
  //   overflow (v, or F2)
  //   The three bit-wise operations do not affect c or v
  //   set z , to true if the result of the operation was zero, otherwise to false.
  //   set s, to b15 of the result
endmodule

module OR (
  input  [4:0] Flags_In,
  input  [15:0] a,
  input  [15:0] b,
  output [4:0] Flags_Out,
  output [15:0] Data_Out
);

  assign Data_Out = a | b;  // OR_Gate or_1, 16 bits wide
  Sign_Flag sign_flag_1 (.Data(Data_Out), .Sign_Out(Flags_Out[0]));
  Zero_Flag zero_flag_1 (.Data(Data_Out), .Zero_Out(Flags_Out[1]));

  assign Flags_Out[4:2] = Flags_In[4:2];

  // Other names for the same wires on the sheet: F0_in = Flags_In[0]; F1_in = Flags_In[1]; F0_out = Flags_Out[0];
  //   F1_out = Flags_Out[1]; F2_in = Flags_In[2]; F3_in = Flags_In[3]; F4_in = Flags_In[4]

  // Notes on the sheet:
  //   sign (s, or F0)
  //   carry-block (F4)
  //   zero (z, or F1)
  //   carry (c, or F3)
  //   overflow (v, or F2)
  //   The three bit-wise operations do not affect c or v
  //   set z , to true if the result of the operation was zero, otherwise to false.
  //   set s, to b15 of the result
endmodule

module XOR (
  input  [4:0] Flags_In,
  input  [15:0] a,
  input  [15:0] b,
  output [4:0] Flags_Out,
  output [15:0] Data_Out
);

  assign Data_Out = a ^ b;  // XOR_Gate xor_1, 16 bits wide
  Sign_Flag sign_flag_1 (.Data(Data_Out), .Sign_Out(Flags_Out[0]));
  Zero_Flag zero_flag_1 (.Data(Data_Out), .Zero_Out(Flags_Out[1]));

  assign Flags_Out[4:2] = Flags_In[4:2];

  // Other names for the same wires on the sheet: F0_in = Flags_In[0]; F1_in = Flags_In[1]; F0_out = Flags_Out[0];
  //   F1_out = Flags_Out[1]; F2_in = Flags_In[2]; F3_in = Flags_In[3]; F4_in = Flags_In[4]

  // Notes on the sheet:
  //   sign (s, or F0)
  //   carry-block (F4)
  //   zero (z, or F1)
  //   carry (c, or F3)
  //   overflow (v, or F2)
  //   The three bit-wise operations do not affect c or v
  //   set z , to true if the result of the operation was zero, otherwise to false.
  //   set s, to b15 of the result
endmodule

module ADD (
  input  [4:0] Flags_In,
  input  [15:0] a,
  input  [15:0] b,
  output [4:0] Flags_Out,
  output [15:0] Data_Out
);

  wire F1_out, multiplexer_1_out;

  Multiplexer #(.enable("false")) multiplexer_1 (
    .in0(Flags_In[3]), .in1(1'b0), .out(multiplexer_1_out), .sel(Flags_In[4]));
  Adder #(.width(16)) adder_1 (.a(a), .b(b), .out(Data_Out), .cin(multiplexer_1_out), .cout(Flags_Out[3]));
  Sign_Flag sign_flag_1 (.Data(Data_Out), .Sign_Out(Flags_Out[0]));
  Zero_Flag zero_flag_1 (.Data(Data_Out), .Zero_Out(F1_out));
  ADD__Overflow_Flag add_overflow_flag_1 (.a(a), .b(b), .write_d(Data_Out), .Overflow_Out(Flags_Out[2]));

  assign {Flags_Out[4], Flags_Out[1]} = {Flags_In[4], Flags_In[1]};

  // Other names for the same wires on the sheet: F0_in = Flags_In[0]; F2_in = Flags_In[2]; F3_in = Flags_In[3];
  //   F0_out = Flags_Out[0]; F1_in = Flags_In[1]; F2_out = Flags_Out[2]; F3_out = Flags_Out[3]; F4_in = Flags_In[4]

  // Notes on the sheet:
  //   sign (s, or F0)
  //   carry-block (F4)
  //   zero (z, or F1)
  //   carry (c, or F3)
  //   overflow (v, or F2)
  //   set c, to true if there was a carry (if the sum/product of the unsigned
  //   interpretation of the operands is greater than or equal to 2^16), and to false otherwise
  //   set s, to b15 of the result
  //   set v, to true if there was a signed-arithemetic overflow
  //   set z , to true if the result of the operation was zero, otherwise to false.
  //   (i.e., if the signed interpretation of bits 15-0 of their result is not equal to the sum
  //   of the signed interpretations of the operands), or to false if there was no overflow.
endmodule

module SUB (
  input  [4:0] Flags_In,
  input  [15:0] a,
  input  [15:0] b,
  output [4:0] Flags_Out,
  output [15:0] Data_Out
);

  wire multiplexer_1_out, not_1_out, subtractor_1_bout;

  not not_1 (not_1_out, Flags_In[3]);
  Multiplexer #(.enable("false")) multiplexer_1 (
    .in0(not_1_out), .in1(1'b0), .out(multiplexer_1_out), .sel(Flags_In[4]));
  Subtractor #(.width(16)) subtractor_1 (
    .a(a), .b(b), .out(Data_Out), .bin(multiplexer_1_out), .bout(subtractor_1_bout));
  not not_2 (Flags_Out[3], subtractor_1_bout);
  Sign_Flag sign_flag_1 (.Data(Data_Out), .Sign_Out(Flags_Out[0]));
  Zero_Flag zero_flag_1 (.Data(Data_Out), .Zero_Out(Flags_Out[1]));
  SUB__Overflow_Flag sub_overflow_flag_1 (.a(a), .b(b), .write_d(Data_Out), .Overflow_Out(Flags_Out[2]));

  assign Flags_Out[4] = Flags_In[4];

  // Other names for the same wires on the sheet: F0_in = Flags_In[0]; F1_in = Flags_In[1]; F2_in = Flags_In[2];
  //   F3_in = Flags_In[3]; F0_out = Flags_Out[0]; F1_out = Flags_Out[1]; F2_out = Flags_Out[2]; F3_out = Flags_Out[3];
  //   F4_in = Flags_In[4]

  // Notes on the sheet:
  //   sign (s, or F0)
  //   carry-block (F4)
  //   zero (z, or F1)
  //   carry (c, or F3)
  //   overflow (v, or F2)
  //   sets c to true if there was  not a need to borrow from the 2^16’s place when subtracting
  //   (i.e., if the unsigned interpretation of  Ra is greater than that of Rb), and to false if there was a need to borrow.
  //   set s, to b15 of the result
  //   set v, to true if there was a signed-arithemetic overflow
  //   set z , to true if the result of the operation was zero, otherwise to false.
  //   (i.e., if the signed interpretation of bits 15-0 of their result is not equal to the sum
  //   of the signed interpretations of the operands), or to false if there was no overflow.
endmodule

module LSL (
  input  [4:0] Flags_In,
  input  [15:0] Data_In,
  output [4:0] Flags_Out,
  output [15:0] Data_Out
);

  Multiplexer #(.enable("false")) multiplexer_1 (.in0(Flags_In[3]), .in1(1'b0), .out(Data_Out[0]), .sel(Flags_In[4]));
  Sign_Flag sign_flag_1 (.Data({Data_In[14:0], Data_Out[0]}), .Sign_Out(Flags_Out[0]));
  Zero_Flag zero_flag_1 (.Data({Data_In[14:0], Data_Out[0]}), .Zero_Out(Flags_Out[1]));

  assign Data_Out[15:1] = Data_In[14:0];
  assign Flags_Out[4:2] = {Flags_In[4], Data_In[15], Flags_In[2]};

  // Other names for the same wires on the sheet: F0_in = Flags_In[0]; F1_in = Flags_In[1]; F3_in = Flags_In[3];
  //   F0_out = Flags_Out[0]; F1_out = Flags_Out[1]; F2_in = Flags_In[2]; F3_out = Data_In[15]; F4_in = Flags_In[4]

  // Notes on the sheet:
  //   c becomes the bit shifted out
  //   sign (s, or F0)
  //   carry-block (F4)
  //   zero (z, or F1)
  //   overflow (v, or F2)
  //   carry (c, or F3)
  //   modify s and z as appropriate for the value produced.
  //   set z , to true if the result of the operation was zero, otherwise to false.
  //   shift in the value (c ∧ F4 ′ ). Thus, when carry-block is false, 
  //   the logical shift operations correspond to a rotate with carry
  //   set s, to b15 of the result
endmodule

module LSR (
  input  [4:0] Flags_In,
  input  [15:0] Data_In,
  output [4:0] Flags_Out,
  output [15:0] Data_Out
);

  Multiplexer #(.enable("false")) multiplexer_1 (.in0(Flags_In[3]), .in1(1'b0), .out(Data_Out[15]), .sel(Flags_In[4]));
  Sign_Flag sign_flag_1 (.Data({Data_Out[15], Data_In[15:1]}), .Sign_Out(Flags_Out[0]));
  Zero_Flag zero_flag_1 (.Data({Data_Out[15], Data_In[15:1]}), .Zero_Out(Flags_Out[1]));

  assign Data_Out[14:0] = Data_In[15:1];
  assign Flags_Out[4:2] = {Flags_In[4], Data_In[0], Flags_In[2]};

  // Other names for the same wires on the sheet: F0_in = Flags_In[0]; F1_in = Flags_In[1]; F3_in = Flags_In[3];
  //   F0_out = Flags_Out[0]; F1_out = Flags_Out[1]; F2_in = Flags_In[2]; F3_out = Data_In[0]; F4_in = Flags_In[4]

  // Notes on the sheet:
  //   shift in the value (c ∧ F4 ′ ). Thus, when carry-block is false, 
  //   the logical shift operations correspond to a rotate with carry
  //   sign (s, or F0)
  //   carry-block (F4)
  //   zero (z, or F1)
  //   overflow (v, or F2)
  //   carry (c, or F3)
  //   modify s and z as appropriate for the value produced.
  //   c becomes the bit shifted out
  //   set z , to true if the result of the operation was zero, otherwise to false.
  //   set s, to b15 of the result
endmodule

module SAVEF (
  input  [4:0] Flags_In,
  output [15:0] Data_Out
);

  assign Data_Out = {{11{1'b0}}, Flags_In};  // Bit_Extender bit_extender_1

  // Other names for the same wires on the sheet: F0_in = Flags_In[0]; F1_in = Flags_In[1]; F2_in = Flags_In[2];
  //   F3_in = Flags_In[3]; F4_in = Flags_In[4]

  // Notes on the sheet:
  //   sign (s, or F0)
  //   carry-block (F4)
  //   zero (z, or F1)
  //   overflow (v, or F2)
  //   carry (c, or F3)
  //   Flags can be collectively saved to a register.
endmodule

module RSTRF (
  input  [15:0] Data,
  output [4:0] Flags_Out
);


  assign Flags_Out = Data[4:0];

  // Other names for the same wires on the sheet: F0_in = Data[0]; F1_in = Data[1]; F2_in = Data[2]; F3_in = Data[3];
  //   F4_in = Data[4]

  // Notes on the sheet:
  //   sign (s, or F0)
  //   carry-block (F4)
  //   zero (z, or F1)
  //   carry (c, or F3)
  //   Flags can be collectively loaded from a register.
  //   overflow (v, or F2)
endmodule

module FON (
  input  [4:0] Flags_In,
  input  [3:0] _11_8,
  input  [3:0] _3_0,
  output [4:0] Flags_Out
);

  Multiplexer #(.enable("false")) multiplexer_1 (.in0(Flags_In[0]), .in1(1'b1), .out(Flags_Out[0]), .sel(_3_0[0]));
  Multiplexer #(.enable("false")) multiplexer_2 (.in0(Flags_In[1]), .in1(1'b1), .out(Flags_Out[1]), .sel(_3_0[1]));
  Multiplexer #(.enable("false")) multiplexer_3 (.in0(Flags_In[2]), .in1(1'b1), .out(Flags_Out[2]), .sel(_3_0[2]));
  Multiplexer #(.enable("false")) multiplexer_4 (.in0(Flags_In[3]), .in1(1'b1), .out(Flags_Out[3]), .sel(_3_0[3]));
  Multiplexer #(.enable("false")) multiplexer_5 (.in0(Flags_In[4]), .in1(1'b1), .out(Flags_Out[4]), .sel(_11_8[0]));

  // Other names for the same wires on the sheet: F0_new = _3_0[0]; F1_new = _3_0[1]; F2_new = _3_0[2];
  //   F3_new = _3_0[3]; F4_new = _11_8[0]; F0_in = Flags_In[0]; F1_in = Flags_In[1]; F2_in = Flags_In[2];
  //   F3_in = Flags_In[3]; F4_in = Flags_In[4]

  // Notes on the sheet:
  //   sign (s, or F0)
  //   carry-block (F4)
  //   zero (z, or F1)
  //   overflow (v, or F2)
  //   carry (c, or F3)
  //   Set to true any flags for which the new values are true
endmodule

module FOFF (
  input  [4:0] Flags_In,
  input  [3:0] _11_8,
  input  [3:0] _3_0,
  output [4:0] Flags_Out
);

  Multiplexer #(.enable("false")) multiplexer_1 (.in0(Flags_In[0]), .in1(1'b0), .out(Flags_Out[0]), .sel(_3_0[0]));
  Multiplexer #(.enable("false")) multiplexer_2 (.in0(Flags_In[1]), .in1(1'b0), .out(Flags_Out[1]), .sel(_3_0[1]));
  Multiplexer #(.enable("false")) multiplexer_3 (.in0(Flags_In[2]), .in1(1'b0), .out(Flags_Out[2]), .sel(_3_0[2]));
  Multiplexer #(.enable("false")) multiplexer_4 (.in0(Flags_In[3]), .in1(1'b0), .out(Flags_Out[3]), .sel(_3_0[3]));
  Multiplexer #(.enable("false")) multiplexer_5 (.in0(Flags_In[4]), .in1(1'b0), .out(Flags_Out[4]), .sel(_11_8[0]));

  // Other names for the same wires on the sheet: F0_new = _3_0[0]; F1_new = _3_0[1]; F2_new = _3_0[2];
  //   F3_new = _3_0[3]; F4_new = _11_8[0]; F0_in = Flags_In[0]; F1_in = Flags_In[1]; F2_in = Flags_In[2];
  //   F3_in = Flags_In[3]; F4_in = Flags_In[4]

  // Notes on the sheet:
  //   sign (s, or F0)
  //   carry-block (F4)
  //   zero (z, or F1)
  //   overflow (v, or F2)
  //   carry (c, or F3)
  //   Set to false any flags for which the new values are true
endmodule

module INC (
  input  [4:0] Flags_In,
  input  [15:0] d,
  input  [7:0] _7_0,
  output [4:0] Flags_Out,
  output [15:0] Data_Out
);

  wire F0_out, F1_out;
  wire [15:0] b, bit_extender_1_out;

  assign bit_extender_1_out = {{10{1'b0}}, _7_0[5:0]};  // Bit_Extender bit_extender_1
  Adder #(.width(16)) adder_1 (.a(bit_extender_1_out), .b(16'h1), .out(b));  // open: cin, cout
  Adder #(.width(16)) adder_2 (.a(d), .b(b), .out(Data_Out), .cout(Flags_Out[3]));  // open: cin
  Sign_Flag sign_flag_1 (.Data(Data_Out), .Sign_Out(F0_out));
  Zero_Flag zero_flag_1 (.Data(Data_Out), .Zero_Out(F1_out));
  ADD__Overflow_Flag add_overflow_flag_1 (.a(d), .b(b), .write_d(Data_Out), .Overflow_Out(Flags_Out[2]));

  assign {Flags_Out[4], Flags_Out[1:0]} = {Flags_In[4], Flags_In[1:0]};

  // Other names for the same wires on the sheet: F2_in = Flags_In[2]; F3_in = Flags_In[3]; F0_in = Flags_In[0];
  //   F1_in = Flags_In[1]; F2_out = Flags_Out[2]; F3_out = Flags_Out[3]; F4_in = Flags_In[4]

  // Notes on the sheet:
  //   sign (s, or F0)
  //   carry-block (F4)
  //   zero (z, or F1)
  //   carry (c, or F3)
  //   overflow (v, or F2)
  //   set c, to true if there was a carry (if the sum/product of the unsigned
  //   interpretation of the operands is greater than or equal to 2^16), and to false otherwise
  //   set s, to b15 of the result
  //   set v, to true if there was a signed-arithemetic overflow
  //   set z , to true if the result of the operation was zero, otherwise to false.
  //   (i.e., if the signed interpretation of bits 15-0 of their result is not equal to the sum
  //   of the signed interpretations of the operands), or to false if there was no overflow.
endmodule

module DEC (
  input  [4:0] Flags_In,
  input  [15:0] d,
  input  [7:0] _7_0,
  output [4:0] Flags_Out,
  output [15:0] Data_Out
);

  wire subtractor_1_bout;
  wire [15:0] b, bit_extender_1_out;

  assign bit_extender_1_out = {{10{1'b0}}, _7_0[5:0]};  // Bit_Extender bit_extender_1
  Adder #(.width(16)) adder_1 (.a(bit_extender_1_out), .b(16'h1), .out(b));  // open: cin, cout
  Subtractor #(.width(16)) subtractor_1 (.a(d), .b(b), .out(Data_Out), .bout(subtractor_1_bout));  // open: bin
  not not_1 (Flags_Out[3], subtractor_1_bout);
  Sign_Flag sign_flag_1 (.Data(Data_Out), .Sign_Out(Flags_Out[0]));
  Zero_Flag zero_flag_1 (.Data(Data_Out), .Zero_Out(Flags_Out[1]));
  SUB__Overflow_Flag sub_overflow_flag_1 (.a(d), .b(b), .write_d(Data_Out), .Overflow_Out(Flags_Out[2]));

  assign Flags_Out[4] = Flags_In[4];

  // Other names for the same wires on the sheet: F0_in = Flags_In[0]; F1_in = Flags_In[1]; F2_in = Flags_In[2];
  //   F3_in = Flags_In[3]; F0_out = Flags_Out[0]; F1_out = Flags_Out[1]; F2_out = Flags_Out[2]; F3_out = Flags_Out[3];
  //   F4_in = Flags_In[4]

  // Notes on the sheet:
  //   sign (s, or F0)
  //   carry-block (F4)
  //   zero (z, or F1)
  //   overflow (v, or F2)
  //   carry (c, or F3)
  //   sets c to true if there was  not a need to borrow from the 2^16’s place when subtracting
  //   (i.e., if the unsigned interpretation of  Ra is greater than that of Rb), and to false if there was a need to borrow.
  //   set s, to b15 of the result
  //   set v, to true if there was a signed-arithemetic overflow
  //   set z , to true if the result of the operation was zero, otherwise to false.
  //   (i.e., if the signed interpretation of bits 15-0 of their result is not equal to the sum
  //   of the signed interpretations of the operands), or to false if there was no overflow.
endmodule

module MUL (
  input  [4:0] Flags_In,
  input  [15:0] a,
  input  [15:0] b,
  output [4:0] Flags_Out,
  output [15:0] Data_Out
);

  wire and_1_out;
  wire [15:0] High_Word, Low_Word;

  Multiplier #(.width(16)) multiplier_1 (.a(a), .b(b), .out(Low_Word), .cout(High_Word));  // open: cin
  and and_1 (and_1_out, Flags_In[0], ~Flags_In[1], ~Flags_In[2], ~Flags_In[3], ~Flags_In[4]);  // AND_Gate
  Multiplexer #(.width(16), .enable("false")) multiplexer_1 (
    .in0(Low_Word), .in1(High_Word), .out(Data_Out), .sel(and_1_out));
  Sign_Flag sign_flag_1 (.Data(Data_Out), .Sign_Out(Flags_Out[0]));
  Zero_Flag zero_flag_1 (.Data(Data_Out), .Zero_Out(Flags_Out[1]));
  MUL__Overflow_Flag mul_overflow_flag_1 (.a(a), .b(b), .write_d(Data_Out), .Overflow_Out(Flags_Out[2]));
  MUL__Carry mul_carry_1 (.High_Word(High_Word), .Carry_Out(Flags_Out[3]));

  assign Flags_Out[4] = Flags_In[4];

  // Other names for the same wires on the sheet: F0_in = Flags_In[0]; F1_in = Flags_In[1]; F2_in = Flags_In[2];
  //   F3_in = Flags_In[3]; F0_out = Flags_Out[0]; F1_out = Flags_Out[1]; F2_out = Flags_Out[2]; F3_out = Flags_Out[3];
  //   F4_in = Flags_In[4]

  // Notes on the sheet:
  //   sign (s, or F0)
  //   carry-block (F4)
  //   zero (z, or F1)
  //   carry (c, or F3)
  //   overflow (v, or F2)
  //   MUL can produce a variety of different results, depending on the values of all four  other flags.
  //   When all are zero, MUL produces produces the low word (bits 15-0) of the product of Ra and Rb, exactly as it does when carry-block is true.
  //   When only s is true, MUL produces the high word (bits 31-16) of the signed interpretations of Ra and Rb.
  //   Carry - highword >0
  //   set s, to b15 of the result
  //   set z , to true if the result of the operation was zero, otherwise to false.
  //   set v, to true if there was a signed-arithemetic overflow
  //   (i.e., if the signed interpretation of bits 15-0 of their result is not equal to the product
  //   of the signed interpretations of the operands), or to false if there was no overflow.
endmodule

module FSET5 (
  input  [3:0] _11_8,
  input  [3:0] _3_0,
  output [4:0] Flags_Out
);


  assign Flags_Out = {_11_8[0], _3_0};

  // Other names for the same wires on the sheet: F0_new = _3_0[0]; F1_new = _3_0[1]; F2_new = _3_0[2];
  //   F3_new = _3_0[3]; F4_new = _11_8[0]

  // Notes on the sheet:
  //   Set all flags to have the values of v
endmodule

module FSET4 (
  input  [4:0] Flags_In,
  input  [3:0] _3_0,
  output [4:0] Flags_Out
);


  assign Flags_Out = {Flags_In[4], _3_0};

  // Other names for the same wires on the sheet: F0_in = Flags_In[0]; F1_in = Flags_In[1]; F2_in = Flags_In[2];
  //   F3_in = Flags_In[3]; F0_new = _3_0[0]; F1_new = _3_0[1]; F2_new = _3_0[2]; F3_new = _3_0[3];
  //   F4_in = Flags_In[4]

  // Notes on the sheet:
  //   sign (s, or F0)
  //   carry-block (F4)
  //   zero (z, or F1)
  //   overflow (v, or F2)
  //   carry (c, or F3)
  //   Set all flags to have the values of v except carry block
endmodule

module ASL (
  input  [4:0] Flags_In,
  input  [15:0] Data_In,
  output [4:0] Flags_Out,
  output [15:0] Data_Out
);

  wire [15:0] adder_1_out;

  Multiplexer #(.enable("false")) multiplexer_1 (.in0(Flags_In[3]), .in1(1'b0), .out(Data_Out[0]), .sel(Flags_In[4]));
  Adder #(.width(16)) adder_1 (.a(Data_In), .b(Data_In), .out(adder_1_out));  // open: cin, cout
  Sign_Flag sign_flag_1 (.Data({Data_In[14:0], Data_Out[0]}), .Sign_Out(Flags_Out[0]));
  Zero_Flag zero_flag_1 (.Data({Data_In[14:0], Data_Out[0]}), .Zero_Out(Flags_Out[1]));
  ADD__Overflow_Flag add_overflow_flag_1 (.a(Data_In), .b(Data_In), .write_d(adder_1_out), .Overflow_Out(Flags_Out[2]));

  assign Data_Out[15:1] = Data_In[14:0];
  assign Flags_Out[4:3] = {Flags_In[4], Data_In[15]};

  // Other names for the same wires on the sheet: F0_in = Flags_In[0]; F1_in = Flags_In[1]; F2_in = Flags_In[2];
  //   F3_in = Flags_In[3]; F0_out = Flags_Out[0]; F1_out = Flags_Out[1]; F2_out = Flags_Out[2]; F3_out = Data_In[15];
  //   F4_in = Flags_In[4]

  // Notes on the sheet:
  //   c becomes the bit shifted out
  //   sign (s, or F0)
  //   carry-block (F4)
  //   zero (z, or F1)
  //   overflow (v, or F2)
  //   carry (c, or F3)
  //   v receives the value it would have after ADD(d,b,b); other-wise the flag values are not changed by shift instructions
  //   modify s and z as appropriate for the value produced.
  //   set z , to true if the result of the operation was zero, otherwise to false.
  //   shift in the value (c ∧ F4 ′ ). Thus, when carry-block is false, 
  //   the logical shift operations correspond to a rotate with carry
  //   set s, to b15 of the result
endmodule

module ASR (
  input  [4:0] Flags_In,
  input  [15:0] Data_In,
  output [4:0] Flags_Out,
  output [15:0] Data_Out
);

  Shifter #(.width(16), .shift("ar")) shifter_1 (.in(Data_In), .\dist (4'b0001), .out(Data_Out));
  Sign_Flag sign_flag_1 (.Data(Data_Out), .Sign_Out(Flags_Out[0]));
  Zero_Flag zero_flag_1 (.Data(Data_Out), .Zero_Out(Flags_Out[1]));

  assign Flags_Out[4:2] = {Flags_In[4], Data_In[0], Flags_In[2]};

  // Other names for the same wires on the sheet: F0_in = Flags_In[0]; F1_in = Flags_In[1]; F3_in = Flags_In[3];
  //   F0_out = Flags_Out[0]; F1_out = Flags_Out[1]; F2_in = Flags_In[2]; F3_out = Data_In[0]; F4_in = Flags_In[4]

  // Notes on the sheet:
  //   c becomes the bit shifted out
  //   ASR ignores the incoming carry, 
  //   always producing a result that is 1/2 the (signed) value.
  //   sign (s, or F0)
  //   carry-block (F4)
  //   zero (z, or F1)
  //   overflow (v, or F2)
  //   carry (c, or F3)
  //   modify s and z as appropriate for the value produced.
  //   set z , to true if the result of the operation was zero, otherwise to false.
  //   set s, to b15 of the result
endmodule

module LSL8 (
  input  [4:0] Flags_In,
  input  [15:0] Data_In,
  output [4:0] Flags_Out,
  output [15:0] Data_Out
);

  Shifter #(.width(16)) shifter_1 (.in(Data_In), .\dist (4'b1000), .out(Data_Out));
  Sign_Flag sign_flag_1 (.Data(Data_Out), .Sign_Out(Flags_Out[0]));
  Zero_Flag zero_flag_1 (.Data(Data_Out), .Zero_Out(Flags_Out[1]));

  assign Flags_Out[4:2] = Flags_In[4:2];

  // Other names for the same wires on the sheet: F0_in = Flags_In[0]; F1_in = Flags_In[1]; F0_out = Flags_Out[0];
  //   F1_out = Flags_Out[1]; F2_in = Flags_In[2]; F3_in = Flags_In[3]; F4_in = Flags_In[4]

  // Notes on the sheet:
  //   sign (s, or F0)
  //   carry-block (F4)
  //   The eight-bit shift operations shift in zeros, regardless of the carry block flag.
  //   zero (z, or F1)
  //   overflow (v, or F2)
  //   carry (c, or F3)
  //   modify s and z as appropriate for the value produced.
  //   set z , to true if the result of the operation was zero, otherwise to false.
  //   set s, to b15 of the result
endmodule

module LSR8 (
  input  [4:0] Flags_In,
  input  [15:0] Data_In,
  output [4:0] Flags_Out,
  output [15:0] Data_Out
);

  Shifter #(.width(16), .shift("lr")) shifter_1 (.in(Data_In), .\dist (4'b1000), .out(Data_Out));
  Sign_Flag sign_flag_1 (.Data(Data_Out), .Sign_Out(Flags_Out[0]));
  Zero_Flag zero_flag_1 (.Data(Data_Out), .Zero_Out(Flags_Out[1]));

  assign Flags_Out[4:2] = Flags_In[4:2];

  // Other names for the same wires on the sheet: F0_in = Flags_In[0]; F1_in = Flags_In[1]; F0_out = Flags_Out[0];
  //   F1_out = Flags_Out[1]; F2_in = Flags_In[2]; F3_in = Flags_In[3]; F4_in = Flags_In[4]

  // Notes on the sheet:
  //   sign (s, or F0)
  //   carry-block (F4)
  //   The eight-bit shift operations shift in zeros, regardless of the carry block flag.
  //   zero (z, or F1)
  //   overflow (v, or F2)
  //   carry (c, or F3)
  //   modify s and z as appropriate for the value produced.
  //   set z , to true if the result of the operation was zero, otherwise to false.
  //   set s, to b15 of the result
endmodule

module Load_Flags (
  input  [4:0] Flags_In,
  input  [15:0] Load_Write_Data,
  input  ld,
  output [4:0] Flags_Out
);

  wire sign_flag_1_sign_out, zero_flag_1_zero_out;

  Sign_Flag sign_flag_1 (.Data(Load_Write_Data), .Sign_Out(sign_flag_1_sign_out));
  Zero_Flag zero_flag_1 (.Data(Load_Write_Data), .Zero_Out(zero_flag_1_zero_out));
  Multiplexer multiplexer_1 (.in0(Flags_In[0]), .in1(sign_flag_1_sign_out), .out(Flags_Out[0]), .sel(ld), .en(ld));
  Multiplexer multiplexer_2 (.in0(Flags_In[1]), .in1(zero_flag_1_zero_out), .out(Flags_Out[1]), .sel(ld), .en(ld));

  assign Flags_Out[4:2] = Flags_In[4:2];

  // Other names for the same wires on the sheet: F0_in = Flags_In[0]; F1_in = Flags_In[1]; F0_out = Flags_Out[0];
  //   F1_out = Flags_Out[1]; F2_in = Flags_In[2]; F3_in = Flags_In[3]; F4_in = Flags_In[4]; Load = ld

  // Notes on the sheet:
  //   sign (s, or F0)
  //   carry-block (F4)
  //   zero (z, or F1)
  //   overflow (v, or F2)
  //   carry (c, or F3)
endmodule

module I_O (
  input  [15:0] R2,
  input  [15:0] OPCODE,
  output [6:0] TTY0,
  output [6:0] TTY1
);

  wire comparator_1_eq;
  wire [1:0] comparator_2_eq;

  Comparator #(.width(16), .mode("unsigned")) comparator_1 (
    .a(OPCODE), .b(16'h5000), .eq(comparator_1_eq));  // open: gt, lt
  Comparator #(.width(16), .mode("unsigned")) comparator_2 (
    .a(OPCODE), .b(16'h5001), .eq(comparator_2_eq[0]));  // open: gt, lt
  Demultiplexer #(.select(2), .width(7), .enable("false")) demultiplexer_1 (
    .out2(TTY0), .out3(TTY1), .in(R2[6:0]), .sel(comparator_2_eq));  // open: out0, out1
  or or_1 (comparator_2_eq[1], comparator_1_eq, comparator_2_eq[0]);

  // Notes on the sheet:
  //   OPCODE for print to TTY0
  //   OPCODE for print to TTY1
  //   character to be printed
  //   7-bit ASCII value
  //   To TTY0 display
  //   TO TTY1 display
  //   // DMX select bit 1: Pass char to one of the TTY's if the OPCODE matches 5000 or 5001
  //   // DMX select bit 0: TTY1 if the match is with 5001, TTY0 otherwise
endmodule

module GET_CHAR_KEYBOARD (
  input  [15:0] OPCODE,
  input  [6:0] keyboard1_in,
  input  [6:0] keyboard2_in,
  output enable_keyboard0,
  output enable_keyboard1,
  output [15:0] data_out,
  output [3:0] write_address
);

  wire decoder_1_out0, decoder_1_out1, yes_op;
  wire [6:0] multiplexer_1_out;

  Hex_Digit_Display hex_digit_display_1 (.value(OPCODE[15:12]));  // open: dp
  Hex_Digit_Display hex_digit_display_2 (.value(OPCODE[7:4]));  // open: dp
  Hex_Digit_Display hex_digit_display_3 (.value(OPCODE[11:8]));  // open: dp
  Comparator #(.width(12)) comparator_1 (.a(OPCODE[15:4]), .b(12'h520), .eq(yes_op));  // open: gt, lt
  Decoder #(.enable("false")) decoder_1 (.out0(decoder_1_out0), .out1(decoder_1_out1), .sel(OPCODE[0]));
  Multiplexer #(.width(7), .enable("false")) multiplexer_1 (
    .in0(keyboard1_in), .in1(keyboard2_in), .out(multiplexer_1_out), .sel(OPCODE[0]));
  and and_1 (enable_keyboard0, yes_op, decoder_1_out0);
  and and_2 (enable_keyboard1, decoder_1_out1, yes_op);
  assign data_out = {{9{1'b0}}, multiplexer_1_out};  // Bit_Extender bit_extender_1
  Multiplexer #(.width(4), .enable("false")) multiplexer_2 (
    .in0(4'b0000), .in1(4'b0010), .out(write_address), .sel(yes_op));

  // Other names for the same wires on the sheet: op0 = OPCODE[0]; op4_f[11:0] = OPCODE[15:4]

  // Notes on the sheet:
  //   Gets availability of Keyboard and 
  //   determine whether to actually write and enable
  //   choose which one to enable
  //   Convert ascii to 16 bits to be put in a register
  //   always write to 2 unless not opcode
  //   perhaps in the future use opcode to determine which register to write
endmodule

module GET_AVAIL_KEYBOARD (
  input  avail_keyboard0,
  input  avail_keyboard1,
  input  [15:0] opcode,
  output [15:0] data_out,
  output [3:0] write_address
);

  wire multiplexer_1_out;

  Multiplexer #(.enable("false")) multiplexer_1 (
    .in0(avail_keyboard0), .in1(avail_keyboard1), .out(multiplexer_1_out), .sel(opcode[0]));
  assign data_out = {{15{1'b0}}, multiplexer_1_out};  // Bit_Extender bit_extender_1

  assign write_address = 4'b0011;

  // Notes on the sheet:
  //   extends the desired keyboard's availability to 16 bits to be placed in register
  //   always write to R3 for now
  //   perhaps specify the register in the opcode in the future?
endmodule

module daddy (
  input  [15:0] opcode_in,
  input  [3:0] write_addr_avail,
  input  [3:0] write_addr_getchar,
  output [3:0] override_write_addr,
  output do_override_write_addr
);

  wire comparator_1_eq, comparator_2_eq, comparator_3_eq, comparator_4_eq, or_1_out;

  Comparator #(.width(4)) comparator_1 (.a(opcode_in[15:12]), .b(4'b0101), .eq(comparator_1_eq));  // open: gt, lt
  Comparator #(.width(4)) comparator_2 (.a(4'b0010), .b(opcode_in[11:8]), .eq(comparator_2_eq));  // open: gt, lt
  Comparator #(.width(4)) comparator_3 (.a(opcode_in[11:8]), .b(4'b0011), .eq(comparator_3_eq));  // open: gt, lt
  Comparator #(.width(4)) comparator_4 (.a(opcode_in[7:4]), .b(4'b0000), .eq(comparator_4_eq));  // open: gt, lt
  Multiplexer #(.width(4), .enable("false")) multiplexer_1 (
    .in0(write_addr_getchar), .in1(write_addr_avail), .out(override_write_addr), .sel(opcode_in[8]));
  or or_1 (or_1_out, comparator_2_eq, comparator_3_eq);
  and and_1 (do_override_write_addr, comparator_1_eq, or_1_out, comparator_4_eq);

  // Other names for the same wires on the sheet: _8b[3:0] = opcode_in[11:8]; b8 = opcode_in[8];
  //   _47[3:0] = opcode_in[7:4]; cf[3:0] = opcode_in[15:12]; write_addr_getavail[3:0] = write_addr_avail
endmodule

module Interrupts (
  input  [15:0] OPCODE
);

  wire RTI, SWI;
  wire [3:0] undriven;

  Comparator #(.width(16)) comparator_1 (.a({OPCODE[15:4], undriven}), .b(16'h2200), .eq(SWI));  // open: gt, lt
  Comparator #(.width(16)) comparator_2 (.a(OPCODE), .b(16'h2300), .eq(RTI));  // open: gt, lt

  // Notes on the sheet:
  //   SWI
  //   RTI
  //   PC to RAM - hardware
  //   PC from RAM - hardware
  //   -STORE registers, flags, PC values to RAM
  //   Registers to RAM - Use STORE instruction (software)
  //   Flags to RAM - Use SAVEF, STORE instructions (software)
  //   - Print from keyboard to TTY (hardware)
  //   -LOAD registers, flags, PC values from RAM
  //   Registers from RAM - Use LOAD instruction (software)
  //   - Type to keyboard (hardware), branch to interrupt handler (software)
  //   Flags from RAM - Use RSTRF, LOAD instructions (software)
endmodule

module interruptedFlag (
  input  clock,
  input  flag_in,
  output flag_out
);

  D_Flip_Flop d_ff_1 (.clk(clock), .D(flag_in), .Q(flag_out));  // open: Qn, preset, en, reset

  // Other names for the same wires on the sheet: is_interrupted_out = flag_out
endmodule

module interruptController (
  input  start_thread,
  input  thread_switch,
  input  [15:0] next_thread,
  input  clock,
  input  [15:0] handler_loc,
  input  [15:0] saved_PC,
  input  [4:0] saved_flags,
  input  [4:0] Flags_Post_ALSU,
  input  avail,
  input  is_interrupted_flag,
  input  do_branch,
  input  [15:0] next_PC_data,
  input  [15:0] current_PC,
  input  [15:0] opcode,
  output do_load_PC,
  output [15:0] normal_next_PC,
  output [15:0] next_PC_loc,
  output [4:0] Flags,
  output next_is_interrupted_flag,
  output do_interrupt
);

  wire comparator_1_eq, comparator_2_eq, is_RTI, multiplexer_4_out, or_1_out;
  wire [15:0] adder_1_out, multiplexer_2_out, multiplexer_3_out;

  Comparator #(.width(4)) comparator_1 (.a(4'b0011), .b(opcode[11:8]), .eq(comparator_1_eq));  // open: gt, lt
  Comparator #(.width(4)) comparator_2 (.a(opcode[15:12]), .b(4'b0010), .eq(comparator_2_eq));  // open: gt, lt
  and and_1 (is_RTI, comparator_1_eq, comparator_2_eq);
  and and_2 (do_interrupt, avail, ~is_interrupted_flag);  // AND_Gate
  or or_1 (or_1_out, is_RTI, thread_switch);
  Adder #(.width(16)) adder_1 (.a(current_PC), .b(16'h1), .out(adder_1_out), .cin(1'b0));  // open: cout
  Multiplexer #(.width(16), .enable("false")) multiplexer_1 (
    .in0(adder_1_out), .in1(next_PC_data), .out(normal_next_PC), .sel(do_branch));
  Multiplexer #(.width(16), .enable("false")) multiplexer_2 (
    .in0(normal_next_PC), .in1(saved_PC), .out(multiplexer_2_out), .sel(or_1_out));
  Multiplexer #(.width(16), .enable("false")) multiplexer_3 (
    .in0(multiplexer_2_out), .in1(handler_loc), .out(multiplexer_3_out), .sel(do_interrupt));
  Multiplexer #(.enable("false")) multiplexer_4 (
    .in0(is_interrupted_flag), .in1(1'b0), .out(multiplexer_4_out), .sel(is_RTI));
  Multiplexer #(.width(16), .enable("false")) multiplexer_5 (
    .in0(multiplexer_3_out), .in1(next_thread), .out(next_PC_loc), .sel(start_thread));
  Multiplexer #(.width(5), .enable("false")) multiplexer_6 (
    .in0(Flags_Post_ALSU), .in1(saved_flags), .out(Flags), .sel(is_RTI));
  or or_2 (do_load_PC, do_branch, is_RTI, do_interrupt, thread_switch);
  Multiplexer #(.enable("false")) multiplexer_7 (
    .in0(multiplexer_4_out), .in1(1'b1), .out(next_is_interrupted_flag), .sel(do_interrupt));

  // Other names for the same wires on the sheet: CLK = clock

  // Notes on the sheet:
  //   when we're not already interrupted, but keyboard has a interrupt signal, we interrupt
  //   also, make sure handler location is saved before we try to interrupt
  //   always output the next normal pc, and save it only if do_interrupt is true
  //   if opcode is Return from interrupt (RTI), next PC should be the saved PC
  //   if do_interrupt, then next PC is the handler location
  //   otherwise, PC should be as normal
  //   if opcode is Return from interrupt (RTI), flags should be set to saved flags
  //   otherwise, defer to ALSU
  //   if opcode is Return from interrupt (RTI), next flag is 0
  //   if do_interrupt, then next flag is 1
  //   otherwise, keep the previous flag
  //   load PC if branching or interrupting or restoring
endmodule

module restore_register (
  input  thread_switch,
  input  [15:0] opcode,
  input  [15:0] data_normal,
  input  enable_normal,
  input  [15:0] data_saved,
  output [15:0] data_out,
  output enable_out
);

  wire comparator_1_eq, do_restore;

  Comparator #(.width(16)) comparator_1 (.a(16'h2300), .b(opcode), .eq(comparator_1_eq));  // open: gt, lt
  or or_1 (do_restore, thread_switch, comparator_1_eq);
  Multiplexer #(.width(16), .enable("false")) multiplexer_1 (
    .in0(data_normal), .in1(data_saved), .out(data_out), .sel(do_restore));
  Multiplexer #(.enable("false")) multiplexer_2 (
    .in0(enable_normal), .in1(do_restore), .out(enable_out), .sel(do_restore));

  // Other names for the same wires on the sheet: normal_data[15:0] = data_normal; saved_data[15:0] = data_saved
endmodule

module shadow (
  input  [15:0] in_R1,
  input  [15:0] in_R2,
  input  [15:0] in_R3,
  input  [15:0] in_R4,
  input  [15:0] in_R5,
  input  [15:0] in_R6,
  input  [15:0] in_R7,
  input  [15:0] in_R8,
  input  [15:0] in_R9,
  input  [15:0] in_Ra,
  input  [15:0] in_Rb,
  input  [15:0] in_Rc,
  input  [15:0] in_Rd,
  input  [15:0] in_Re,
  input  [15:0] in_Rf,
  input  [4:0] flags_to_save,
  input  [15:0] pc_to_save,
  input  do_interrupt,
  input  thread_switch,
  input  CLOCK,
  input  [15:0] opcode,
  output [4:0] saved_flags_out,
  output [15:0] saved_PC_out,
  output firstswitch,
  output [15:0] handler_out,
  output [15:0] out_R1,
  output [15:0] out_R2,
  output [15:0] out_R3,
  output [15:0] out_R4,
  output [15:0] out_R5,
  output [15:0] out_R6,
  output [15:0] out_R7,
  output [15:0] out_R8,
  output [15:0] out_R9,
  output [15:0] out_Ra,
  output [15:0] out_Rb,
  output [15:0] out_Rc,
  output [15:0] out_Rd,
  output [15:0] out_Re,
  output [15:0] out_Rf
);

  wire and_1_out, comparator_1_eq, comparator_2_eq, comparator_3_eq, comparator_4_eq, comparator_5_eq,
       comparator_6_eq, enable_save, not_1_out, or_1_out, save_handler, save_now;
  wire [15:0] multiplexer_1_out, saved_PC_q;

  or or_1 (or_1_out, do_interrupt, thread_switch);
  Multiplexer #(.select(4), .width(16)) multiplexer_1 (
    .in0({16{1'b0}}), .in1(in_R1), .in2(in_R2), .in3(in_R3), .in4(in_R4), .in5(in_R5), .in6(in_R6),
    .in7(in_R7), .in8(in_R8), .in9(in_R9), .in10(in_Ra), .in11(in_Rb), .in12(in_Rc), .in13(in_Rd),
    .in14(in_Re), .in15(in_Rf), .out(multiplexer_1_out), .sel(opcode[3:0]));  // open: en
  Register #(.width(5)) saved_flags (.D(flags_to_save), .en(save_now), .Q(saved_flags_out), .clk(CLOCK));  // open: clr
  Multiplexer #(.width(16), .enable("false")) multiplexer_2 (
    .in0(saved_PC_q), .in1(16'h2), .out(saved_PC_out), .sel(not_1_out));
  Register #(.width(16)) saved_PC (.D(pc_to_save), .en(or_1_out), .Q(saved_PC_q), .clk(CLOCK));  // open: clr
  not not_1 (not_1_out, firstswitch);
  Register #(.width(16)) handler_loc (
    .D(multiplexer_1_out), .en(save_handler), .Q(handler_out), .clk(CLOCK));  // open: clr
  D_Flip_Flop d_ff_1 (.clk(CLOCK), .D(1'b1), .Q(firstswitch), .en(and_1_out));  // open: Qn, preset, reset
  and and_1 (and_1_out, thread_switch, ~firstswitch);  // AND_Gate
  Comparator #(.width(4)) comparator_1 (.a(4'b0110), .b(opcode[15:12]), .eq(comparator_1_eq));  // open: gt, lt
  Comparator #(.width(4)) comparator_2 (.a(4'b0000), .b(opcode[11:8]), .eq(comparator_2_eq));  // open: gt, lt
  Comparator #(.width(4)) comparator_3 (.a(4'b0000), .b(opcode[7:4]), .eq(comparator_3_eq));  // open: gt, lt
  and and_2 (save_handler, comparator_1_eq, comparator_2_eq, comparator_3_eq);
  Register #(.width(16)) r1_copy (.D(in_R1), .en(save_now), .Q(out_R1), .clk(CLOCK));  // open: clr
  Register #(.width(16)) r2_copy (.D(in_R2), .en(save_now), .Q(out_R2), .clk(CLOCK));  // open: clr
  Register #(.width(16)) r3_copy (.D(in_R3), .en(save_now), .Q(out_R3), .clk(CLOCK));  // open: clr
  Register #(.width(16)) r4_copy (.D(in_R4), .en(save_now), .Q(out_R4), .clk(CLOCK));  // open: clr
  Register #(.width(16)) r5_copy (.D(in_R5), .en(save_now), .Q(out_R5), .clk(CLOCK));  // open: clr
  Register #(.width(16)) r6_copy (.D(in_R6), .en(save_now), .Q(out_R6), .clk(CLOCK));  // open: clr
  Register #(.width(16)) r7_copy (.D(in_R7), .en(save_now), .Q(out_R7), .clk(CLOCK));  // open: clr
  Register #(.width(16)) r8_copy (.D(in_R8), .en(save_now), .Q(out_R8), .clk(CLOCK));  // open: clr
  Register #(.width(16)) r9_copy (.D(in_R9), .en(save_now), .Q(out_R9), .clk(CLOCK));  // open: clr
  Register #(.width(16)) ra_copy (.D(in_Ra), .en(save_now), .Q(out_Ra), .clk(CLOCK));  // open: clr
  Register #(.width(16)) rb_copy (.D(in_Rb), .en(save_now), .Q(out_Rb), .clk(CLOCK));  // open: clr
  Register #(.width(16)) rc_copy (.D(in_Rc), .en(save_now), .Q(out_Rc), .clk(CLOCK));  // open: clr
  Register #(.width(16)) rd_copy (.D(in_Rd), .en(save_now), .Q(out_Rd), .clk(CLOCK));  // open: clr
  Register #(.width(16)) re_copy (.D(in_Re), .en(save_now), .Q(out_Re), .clk(CLOCK));  // open: clr
  Register #(.width(16)) rf_copy (.D(in_Rf), .en(save_now), .Q(out_Rf), .clk(CLOCK));  // open: clr
  Comparator #(.width(4)) comparator_4 (.a(4'b0010), .b(opcode[15:12]), .eq(comparator_4_eq));  // open: gt, lt
  and and_3 (enable_save, comparator_4_eq, comparator_5_eq, comparator_6_eq);
  Comparator #(.width(4)) comparator_5 (.a(4'b0010), .b(opcode[11:8]), .eq(comparator_5_eq));  // open: gt, lt
  Comparator #(.width(4)) comparator_6 (.a(4'b0000), .b(opcode[7:4]), .eq(comparator_6_eq));  // open: gt, lt
  or or_2 (save_now, enable_save, thread_switch);

  // Other names for the same wires on the sheet: op03[3:0] = opcode[3:0]; op47[3:0] = opcode[7:4];
  //   op8b[3:0] = opcode[11:8]; opcf[3:0] = opcode[15:12]

  // Notes on the sheet:
  //   store register address by opcode bits 0-3 to handler
  //   only if opcode is 0x600d
endmodule

module thread_init (
  input  [15:0] OPCODE,
  output start_thread,
  output [15:0] thread_PC
);

  assign thread_PC = {{8{1'b0}}, OPCODE[7:0]};  // Bit_Extender bit_extender_1
  Comparator comparator_1 (.a(OPCODE[15:8]), .b(8'h88), .eq(start_thread));  // open: gt, lt
endmodule

module Multithreading (
  input  start_thread,
  input  CLK,
  input  [15:0] thread_PC,
  output thread_switch,
  output [15:0] next_thread
);

  wire not_1_out;
  wire [3:0] random_1_out;
  wire [15:0] counter_1_q, counter_2_q, multiplexer_1_out;

  Random #(.width(4)) random_1 (.clk(CLK), .out(random_1_out));  // open: next, clr
  Comparator #(.width(4), .mode("unsigned")) comparator_1 (
    .a(4'b1101), .b(random_1_out), .lt(thread_switch));  // open: gt, eq
  Counter #(.width(16), .max('h1)) counter_1 (
    .count(thread_switch), .Q(counter_1_q), .clk(CLK));  // open: load, D, carry, clr
  Counter #(.width(16), .max('hffff)) counter_2 (
    .count(start_thread), .Q(counter_2_q), .clk(CLK));  // open: load, D, carry, clr
  Multiplexer #(.width(16), .enable("false")) multiplexer_1 (
    .in0(counter_1_q), .in1(counter_2_q), .out(multiplexer_1_out), .sel(start_thread));
  not not_1 (not_1_out, start_thread);
  RAM #(.addrWidth(16), .dataWidth(16)) ram_1 (
    .addr(multiplexer_1_out), .data(next_thread), .clk(CLK), .ld(not_1_out));  // open: sel, clr
  assign next_thread = start_thread ? thread_PC : 16'bz;  // Controlled_Buffer controlled_buffer_1
endmodule
